// Logisim project ProjetoBancoReg.circ as structural Verilog: 8 circuits, main circuit main
module main (
  input  in_1,
  input  in_2,
  input  in_3,
  input  in_4,
  input  reset,
  input  reset_2,
  output out_7,
  output out_8,
  output out_9,
  output out_10
);

  D_Flip_Flop d_ff_1 (.clk(reset), .D(in_1), .Q(out_7), .reset(reset_2));  // open: Qn, preset, en
  D_Flip_Flop d_ff_2 (.clk(reset), .D(in_2), .Q(out_8), .reset(reset_2));  // open: Qn, preset, en
  D_Flip_Flop d_ff_3 (.clk(reset), .D(in_3), .Q(out_9), .reset(reset_2));  // open: Qn, preset, en
  D_Flip_Flop d_ff_4 (.clk(reset), .D(in_4), .Q(out_10), .reset(reset_2));  // open: Qn, preset, en
endmodule

module BancoReg4bit (
  input  [3:0] INPUT,
  input  SAVE,
  input  Reset,
  output [3:0] OUT
);

  D_Flip_Flop d_ff_1 (.clk(SAVE), .D(INPUT[3]), .Q(OUT[3]), .reset(Reset));  // open: Qn, preset, en
  D_Flip_Flop d_ff_2 (.clk(SAVE), .D(INPUT[2]), .Q(OUT[2]), .reset(Reset));  // open: Qn, preset, en
  D_Flip_Flop d_ff_3 (.clk(SAVE), .D(INPUT[1]), .Q(OUT[1]), .reset(Reset));  // open: Qn, preset, en
  D_Flip_Flop d_ff_4 (.clk(SAVE), .D(INPUT[0]), .Q(OUT[0]), .reset(Reset));  // open: Qn, preset, en
endmodule

module Registrador4bits (
  input  [3:0] in_1,
  input  in_2,
  input  in_3,
  input  in_4,
  input  in_5,
  input  in_6,
  input  in_7,
  input  in_8,
  input  in_9,
  input  in_10,
  output [3:0] out_11,
  output [3:0] out_12,
  output [3:0] out_13,
  output [3:0] out_14,
  output [3:0] out_15,
  output [3:0] out_16,
  output [3:0] out_17,
  output [3:0] out_18
);

  BancoReg4bit bancoreg4bit_1 (.SAVE(in_2), .Reset(in_3), .OUT(out_11), .INPUT(in_1));
  BancoReg4bit bancoreg4bit_2 (.SAVE(in_4), .Reset(in_3), .OUT(out_12), .INPUT(in_1));
  BancoReg4bit bancoreg4bit_3 (.SAVE(in_5), .Reset(in_3), .OUT(out_13), .INPUT(in_1));
  BancoReg4bit bancoreg4bit_4 (.SAVE(in_6), .Reset(in_3), .OUT(out_14), .INPUT(in_1));
  BancoReg4bit bancoreg4bit_5 (.SAVE(in_7), .Reset(in_3), .OUT(out_15), .INPUT(in_1));
  BancoReg4bit bancoreg4bit_6 (.SAVE(in_8), .Reset(in_3), .OUT(out_16), .INPUT(in_1));
  BancoReg4bit bancoreg4bit_7 (.SAVE(in_9), .Reset(in_3), .OUT(out_17), .INPUT(in_1));
  BancoReg4bit bancoreg4bit_8 (.SAVE(in_10), .Reset(in_3), .OUT(out_18), .INPUT(in_1));
endmodule

module BancoReg4bits (
  input  [3:0] Data,
  input  Reset,
  input  [2:0] RegA,
  input  CLK,
  input  [2:0] WReg,
  input  [2:0] RegB,
  output [3:0] ViewRegA,
  output [3:0] ViewRegB
);

  wire demultiplexer_1_out0, demultiplexer_1_out1, demultiplexer_1_out2, demultiplexer_1_out3,
       demultiplexer_1_out4, demultiplexer_1_out5, demultiplexer_1_out6, demultiplexer_1_out7;
  wire [3:0] bancoreg4bit_1_out, bancoreg4bit_2_out, bancoreg4bit_3_out, bancoreg4bit_4_out,
       bancoreg4bit_5_out, bancoreg4bit_6_out, bancoreg4bit_7_out, bancoreg4bit_8_out;

  Demultiplexer #(.select(3), .enable("false")) demultiplexer_1 (
    .out0(demultiplexer_1_out0), .out1(demultiplexer_1_out1), .out2(demultiplexer_1_out2),
    .out3(demultiplexer_1_out3), .out4(demultiplexer_1_out4), .out5(demultiplexer_1_out5),
    .out6(demultiplexer_1_out6), .out7(demultiplexer_1_out7), .in(CLK), .sel(WReg));
  Demultiplexer #(.select(3), .enable("false")) demultiplexer_2 (
    .out0(demultiplexer_1_out0), .out1(demultiplexer_1_out1), .out2(demultiplexer_1_out2),
    .out3(demultiplexer_1_out3), .out4(demultiplexer_1_out4), .out5(demultiplexer_1_out5),
    .out6(demultiplexer_1_out6), .out7(demultiplexer_1_out7), .in(CLK), .sel(WReg));
  BancoReg4bit bancoreg4bit_1 (.SAVE(demultiplexer_1_out0), .Reset(Reset), .OUT(bancoreg4bit_1_out), .INPUT(Data));
  BancoReg4bit bancoreg4bit_2 (.SAVE(demultiplexer_1_out1), .Reset(Reset), .OUT(bancoreg4bit_2_out), .INPUT(Data));
  BancoReg4bit bancoreg4bit_3 (.SAVE(demultiplexer_1_out2), .Reset(Reset), .OUT(bancoreg4bit_3_out), .INPUT(Data));
  BancoReg4bit bancoreg4bit_4 (.SAVE(demultiplexer_1_out3), .Reset(Reset), .OUT(bancoreg4bit_4_out), .INPUT(Data));
  BancoReg4bit bancoreg4bit_5 (.SAVE(demultiplexer_1_out4), .Reset(Reset), .OUT(bancoreg4bit_5_out), .INPUT(Data));
  BancoReg4bit bancoreg4bit_6 (.SAVE(demultiplexer_1_out5), .Reset(Reset), .OUT(bancoreg4bit_6_out), .INPUT(Data));
  BancoReg4bit bancoreg4bit_7 (.SAVE(demultiplexer_1_out6), .Reset(Reset), .OUT(bancoreg4bit_7_out), .INPUT(Data));
  BancoReg4bit bancoreg4bit_8 (.SAVE(demultiplexer_1_out7), .Reset(Reset), .OUT(bancoreg4bit_8_out), .INPUT(Data));
  Multiplexer #(.select(3), .width(4), .enable("false")) multiplexer_1 (
    .in0(bancoreg4bit_1_out), .in1(bancoreg4bit_2_out), .in2(bancoreg4bit_3_out), .in3(bancoreg4bit_4_out),
    .in4(bancoreg4bit_5_out), .in5(bancoreg4bit_6_out), .in6(bancoreg4bit_7_out), .in7(bancoreg4bit_8_out),
    .out(ViewRegA), .sel(RegA));
  Multiplexer #(.select(3), .width(4), .enable("false")) multiplexer_2 (
    .in0(bancoreg4bit_1_out), .in1(bancoreg4bit_2_out), .in2(bancoreg4bit_3_out), .in3(bancoreg4bit_4_out),
    .in4(bancoreg4bit_5_out), .in5(bancoreg4bit_6_out), .in6(bancoreg4bit_7_out), .in7(bancoreg4bit_8_out),
    .out(ViewRegB), .sel(RegB));
endmodule

module Registrador32bits (
  input  [31:0] INPUT,
  input  SAVE,
  input  Reset,
  output [31:0] OUT
);

  D_Flip_Flop d_ff_1 (.clk(SAVE), .D(INPUT[31]), .Q(OUT[31]), .reset(Reset));  // open: Qn, preset, en
  D_Flip_Flop d_ff_2 (.D(INPUT[30]), .Q(OUT[30]), .reset(Reset));  // open: clk, Qn, preset, en
  D_Flip_Flop d_ff_3 (.clk(SAVE), .D(INPUT[29]), .Q(OUT[29]), .reset(Reset));  // open: Qn, preset, en
  D_Flip_Flop d_ff_4 (.clk(SAVE), .D(INPUT[28]), .Q(OUT[28]), .reset(Reset));  // open: Qn, preset, en
  D_Flip_Flop d_ff_5 (.clk(SAVE), .D(INPUT[27]), .Q(OUT[27]), .reset(Reset));  // open: Qn, preset, en
  D_Flip_Flop d_ff_6 (.clk(SAVE), .D(INPUT[26]), .Q(OUT[26]), .reset(Reset));  // open: Qn, preset, en
  D_Flip_Flop d_ff_7 (.clk(SAVE), .D(INPUT[25]), .Q(OUT[25]), .reset(Reset));  // open: Qn, preset, en
  D_Flip_Flop d_ff_8 (.clk(SAVE), .D(INPUT[24]), .Q(OUT[24]), .reset(Reset));  // open: Qn, preset, en
  D_Flip_Flop d_ff_9 (.clk(SAVE), .D(INPUT[23]), .Q(OUT[23]), .reset(Reset));  // open: Qn, preset, en
  D_Flip_Flop d_ff_10 (.clk(SAVE), .D(INPUT[22]), .Q(OUT[22]), .reset(Reset));  // open: Qn, preset, en
  D_Flip_Flop d_ff_11 (.clk(SAVE), .D(INPUT[21]), .Q(OUT[21]), .reset(Reset));  // open: Qn, preset, en
  D_Flip_Flop d_ff_12 (.clk(SAVE), .D(INPUT[20]), .Q(OUT[20]), .reset(Reset));  // open: Qn, preset, en
  D_Flip_Flop d_ff_13 (.clk(SAVE), .D(INPUT[19]), .Q(OUT[19]), .reset(Reset));  // open: Qn, preset, en
  D_Flip_Flop d_ff_14 (.clk(SAVE), .D(INPUT[18]), .Q(OUT[18]), .reset(Reset));  // open: Qn, preset, en
  D_Flip_Flop d_ff_15 (.clk(SAVE), .D(INPUT[17]), .Q(OUT[17]), .reset(Reset));  // open: Qn, preset, en
  D_Flip_Flop d_ff_16 (.clk(SAVE), .D(INPUT[16]), .Q(OUT[16]), .reset(Reset));  // open: Qn, preset, en
  D_Flip_Flop d_ff_17 (.clk(SAVE), .D(INPUT[15]), .Q(OUT[15]), .reset(Reset));  // open: Qn, preset, en
  D_Flip_Flop d_ff_18 (.clk(SAVE), .D(INPUT[14]), .Q(OUT[14]), .reset(Reset));  // open: Qn, preset, en
  D_Flip_Flop d_ff_19 (.clk(SAVE), .D(INPUT[13]), .Q(OUT[13]), .reset(Reset));  // open: Qn, preset, en
  D_Flip_Flop d_ff_20 (.clk(SAVE), .D(INPUT[12]), .Q(OUT[12]), .reset(Reset));  // open: Qn, preset, en
  D_Flip_Flop d_ff_21 (.clk(SAVE), .D(INPUT[11]), .Q(OUT[11]), .reset(Reset));  // open: Qn, preset, en
  D_Flip_Flop d_ff_22 (.clk(SAVE), .D(INPUT[10]), .Q(OUT[10]), .reset(Reset));  // open: Qn, preset, en
  D_Flip_Flop d_ff_23 (.clk(SAVE), .D(INPUT[9]), .Q(OUT[9]), .reset(Reset));  // open: Qn, preset, en
  D_Flip_Flop d_ff_24 (.clk(SAVE), .D(INPUT[8]), .Q(OUT[8]), .reset(Reset));  // open: Qn, preset, en
  D_Flip_Flop d_ff_25 (.clk(SAVE), .D(INPUT[7]), .Q(OUT[7]), .reset(Reset));  // open: Qn, preset, en
  D_Flip_Flop d_ff_26 (.clk(SAVE), .D(INPUT[6]), .Q(OUT[6]), .reset(Reset));  // open: Qn, preset, en
  D_Flip_Flop d_ff_27 (.clk(SAVE), .D(INPUT[5]), .Q(OUT[5]), .reset(Reset));  // open: Qn, preset, en
  D_Flip_Flop d_ff_28 (.clk(SAVE), .D(INPUT[4]), .Q(OUT[4]), .reset(Reset));  // open: Qn, preset, en
  D_Flip_Flop d_ff_29 (.clk(SAVE), .D(INPUT[3]), .Q(OUT[3]), .reset(Reset));  // open: Qn, preset, en
  D_Flip_Flop d_ff_30 (.clk(SAVE), .D(INPUT[2]), .Q(OUT[2]), .reset(Reset));  // open: Qn, preset, en
  D_Flip_Flop d_ff_31 (.clk(SAVE), .D(INPUT[1]), .Q(OUT[1]), .reset(Reset));  // open: Qn, preset, en
  D_Flip_Flop d_ff_32 (.clk(SAVE), .D(INPUT[0]), .Q(OUT[0]), .reset(Reset));  // open: Qn, preset, en
endmodule

module BancoReg32bits (
  input  [31:0] Data,
  input  Reset,
  input  [4:0] in_3,
  input  CLK,
  input  [4:0] in_5,
  input  [4:0] wReg,
  output [31:0] ViewRegA,
  output out_8,
  output [31:0] ViewRegB,
  output out_10
);

  wire demultiplexer_1_out0, demultiplexer_1_out1, demultiplexer_1_out2, demultiplexer_1_out3,
       demultiplexer_1_out4, demultiplexer_1_out5, demultiplexer_1_out6, demultiplexer_1_out7,
       demultiplexer_1_out8, demultiplexer_1_out9, demultiplexer_1_out10, demultiplexer_1_out11,
       demultiplexer_1_out12, demultiplexer_1_out13, demultiplexer_1_out14, demultiplexer_1_out15,
       demultiplexer_1_out16, demultiplexer_1_out17, demultiplexer_1_out18, demultiplexer_1_out19,
       demultiplexer_1_out20, demultiplexer_1_out21, demultiplexer_1_out22, demultiplexer_1_out23,
       demultiplexer_1_out24, demultiplexer_1_out25, demultiplexer_1_out26, demultiplexer_1_out27,
       demultiplexer_1_out28, demultiplexer_1_out29, demultiplexer_1_out30, demultiplexer_1_out31;
  wire [31:0] registrador32bits_1_out, registrador32bits_2_out, registrador32bits_3_out,
       registrador32bits_4_out, registrador32bits_5_out, registrador32bits_6_out, registrador32bits_7_out,
       registrador32bits_8_out, registrador32bits_9_out, registrador32bits_10_out, registrador32bits_11_out,
       registrador32bits_12_out, registrador32bits_13_out, registrador32bits_14_out,
       registrador32bits_15_out, registrador32bits_16_out, registrador32bits_17_out,
       registrador32bits_18_out, registrador32bits_19_out, registrador32bits_20_out,
       registrador32bits_21_out, registrador32bits_22_out, registrador32bits_26_out,
       registrador32bits_28_out, registrador32bits_29_out, registrador32bits_30_out,
       registrador32bits_31_out, registrador32bits_32_out;

  Demultiplexer #(.select(5), .enable("false")) demultiplexer_1 (
    .out0(demultiplexer_1_out0), .out1(demultiplexer_1_out1), .out2(demultiplexer_1_out2),
    .out3(demultiplexer_1_out3), .out4(demultiplexer_1_out4), .out5(demultiplexer_1_out5),
    .out6(demultiplexer_1_out6), .out7(demultiplexer_1_out7), .out8(demultiplexer_1_out8),
    .out9(demultiplexer_1_out9), .out10(demultiplexer_1_out10), .out11(demultiplexer_1_out11),
    .out12(demultiplexer_1_out12), .out13(demultiplexer_1_out13), .out14(demultiplexer_1_out14),
    .out15(demultiplexer_1_out15), .out16(demultiplexer_1_out16), .out17(demultiplexer_1_out17),
    .out18(demultiplexer_1_out18), .out19(demultiplexer_1_out19), .out20(demultiplexer_1_out20),
    .out21(demultiplexer_1_out21), .out22(demultiplexer_1_out22), .out23(demultiplexer_1_out23),
    .out24(demultiplexer_1_out24), .out25(demultiplexer_1_out25), .out26(demultiplexer_1_out26),
    .out27(demultiplexer_1_out27), .out28(demultiplexer_1_out28), .out29(demultiplexer_1_out29),
    .out30(demultiplexer_1_out30), .out31(demultiplexer_1_out31), .in(CLK), .sel(in_5));
  Registrador32bits registrador32bits_1 (
    .SAVE(demultiplexer_1_out0), .Reset(Reset), .INPUT(Data), .OUT(registrador32bits_1_out));
  Registrador32bits registrador32bits_2 (
    .SAVE(demultiplexer_1_out1), .Reset(Reset), .INPUT(Data), .OUT(registrador32bits_2_out));
  Registrador32bits registrador32bits_3 (
    .SAVE(demultiplexer_1_out2), .Reset(Reset), .INPUT(Data), .OUT(registrador32bits_3_out));
  Registrador32bits registrador32bits_4 (
    .SAVE(demultiplexer_1_out3), .Reset(Reset), .INPUT(Data), .OUT(registrador32bits_4_out));
  Registrador32bits registrador32bits_5 (
    .SAVE(demultiplexer_1_out4), .Reset(Reset), .INPUT(Data), .OUT(registrador32bits_5_out));
  Registrador32bits registrador32bits_6 (
    .SAVE(demultiplexer_1_out5), .Reset(Reset), .INPUT(Data), .OUT(registrador32bits_6_out));
  Registrador32bits registrador32bits_7 (
    .SAVE(demultiplexer_1_out6), .Reset(Reset), .INPUT(Data), .OUT(registrador32bits_7_out));
  Registrador32bits registrador32bits_8 (
    .SAVE(demultiplexer_1_out7), .Reset(Reset), .INPUT(Data), .OUT(registrador32bits_8_out));
  Registrador32bits registrador32bits_9 (
    .SAVE(demultiplexer_1_out8), .Reset(Reset), .INPUT(Data), .OUT(registrador32bits_9_out));
  Registrador32bits registrador32bits_10 (
    .SAVE(demultiplexer_1_out9), .Reset(Reset), .INPUT(Data), .OUT(registrador32bits_10_out));
  Registrador32bits registrador32bits_11 (
    .SAVE(demultiplexer_1_out10), .Reset(Reset), .INPUT(Data), .OUT(registrador32bits_11_out));
  Registrador32bits registrador32bits_12 (
    .SAVE(demultiplexer_1_out11), .Reset(Reset), .INPUT(Data), .OUT(registrador32bits_12_out));
  Registrador32bits registrador32bits_13 (
    .SAVE(demultiplexer_1_out12), .Reset(Reset), .INPUT(Data), .OUT(registrador32bits_13_out));
  Registrador32bits registrador32bits_14 (
    .SAVE(demultiplexer_1_out13), .Reset(Reset), .INPUT(Data), .OUT(registrador32bits_14_out));
  Registrador32bits registrador32bits_15 (
    .SAVE(demultiplexer_1_out14), .Reset(Reset), .INPUT(Data), .OUT(registrador32bits_15_out));
  Registrador32bits registrador32bits_16 (
    .SAVE(demultiplexer_1_out15), .Reset(Reset), .INPUT(Data), .OUT(registrador32bits_16_out));
  Registrador32bits registrador32bits_17 (
    .SAVE(demultiplexer_1_out16), .Reset(Reset), .INPUT(Data), .OUT(registrador32bits_17_out));
  Registrador32bits registrador32bits_18 (
    .SAVE(demultiplexer_1_out17), .Reset(Reset), .INPUT(Data), .OUT(registrador32bits_18_out));
  Registrador32bits registrador32bits_19 (
    .SAVE(demultiplexer_1_out18), .Reset(Reset), .INPUT(Data), .OUT(registrador32bits_19_out));
  Registrador32bits registrador32bits_20 (
    .SAVE(demultiplexer_1_out19), .Reset(Reset), .INPUT(Data), .OUT(registrador32bits_20_out));
  Registrador32bits registrador32bits_21 (
    .SAVE(demultiplexer_1_out20), .Reset(Reset), .INPUT(Data), .OUT(registrador32bits_21_out));
  Registrador32bits registrador32bits_22 (
    .SAVE(demultiplexer_1_out21), .Reset(Reset), .INPUT(Data), .OUT(registrador32bits_22_out));
  Registrador32bits registrador32bits_23 (
    .SAVE(demultiplexer_1_out22), .Reset(Reset), .INPUT(Data), .OUT(registrador32bits_6_out));
  Registrador32bits registrador32bits_24 (
    .SAVE(demultiplexer_1_out23), .Reset(Reset), .INPUT(Data), .OUT(registrador32bits_13_out));
  Registrador32bits registrador32bits_25 (
    .SAVE(demultiplexer_1_out24), .Reset(Reset), .INPUT(Data), .OUT(registrador32bits_20_out));
  Registrador32bits registrador32bits_26 (
    .SAVE(demultiplexer_1_out25), .Reset(Reset), .INPUT(Data), .OUT(registrador32bits_26_out));
  Registrador32bits registrador32bits_27 (
    .SAVE(demultiplexer_1_out26), .Reset(Reset), .INPUT(Data), .OUT(registrador32bits_26_out));
  Registrador32bits registrador32bits_28 (
    .SAVE(demultiplexer_1_out27), .Reset(Reset), .INPUT(Data), .OUT(registrador32bits_28_out));
  Registrador32bits registrador32bits_29 (
    .SAVE(demultiplexer_1_out28), .Reset(Reset), .INPUT(Data), .OUT(registrador32bits_29_out));
  Registrador32bits registrador32bits_30 (
    .SAVE(demultiplexer_1_out29), .Reset(Reset), .INPUT(Data), .OUT(registrador32bits_30_out));
  Registrador32bits registrador32bits_31 (
    .SAVE(demultiplexer_1_out30), .Reset(Reset), .INPUT(Data), .OUT(registrador32bits_31_out));
  Registrador32bits registrador32bits_32 (
    .SAVE(demultiplexer_1_out31), .Reset(Reset), .INPUT(Data), .OUT(registrador32bits_32_out));
  Multiplexer #(.select(5), .width(32), .enable("false")) multiplexer_1 (
    .in0(registrador32bits_1_out), .in1(registrador32bits_2_out), .in2(registrador32bits_3_out),
    .in3(registrador32bits_4_out), .in4(registrador32bits_5_out), .in5(registrador32bits_6_out),
    .in6(registrador32bits_7_out), .in7(registrador32bits_8_out), .in8(registrador32bits_9_out),
    .in9(registrador32bits_10_out), .in10(registrador32bits_11_out), .in11(registrador32bits_12_out),
    .in12(registrador32bits_13_out), .in13(registrador32bits_14_out), .in14(registrador32bits_15_out),
    .in15(registrador32bits_16_out), .in16(registrador32bits_17_out), .in17(registrador32bits_18_out),
    .in18(registrador32bits_19_out), .in19(registrador32bits_20_out), .in20(registrador32bits_21_out),
    .in21(registrador32bits_22_out), .in22(registrador32bits_6_out), .in23(registrador32bits_13_out),
    .in24(registrador32bits_20_out), .in25(registrador32bits_26_out), .in26(registrador32bits_26_out),
    .in27(registrador32bits_28_out), .in28(registrador32bits_29_out), .in29(registrador32bits_30_out),
    .in30(registrador32bits_31_out), .in31(registrador32bits_32_out), .out(ViewRegA), .sel(in_3));
  Multiplexer #(.select(5), .width(32), .enable("false")) multiplexer_2 (
    .in0(registrador32bits_1_out), .in1(registrador32bits_2_out), .in2(registrador32bits_3_out),
    .in3(registrador32bits_4_out), .in4(registrador32bits_5_out), .in5(registrador32bits_6_out),
    .in6(registrador32bits_7_out), .in7(registrador32bits_8_out), .in8(registrador32bits_9_out),
    .in9(registrador32bits_10_out), .in10(registrador32bits_11_out), .in11(registrador32bits_12_out),
    .in12(registrador32bits_13_out), .in13(registrador32bits_14_out), .in14(registrador32bits_15_out),
    .in15(registrador32bits_16_out), .in16(registrador32bits_17_out), .in17(registrador32bits_18_out),
    .in18(registrador32bits_19_out), .in19(registrador32bits_20_out), .in20(registrador32bits_21_out),
    .in21(registrador32bits_22_out), .in22(registrador32bits_6_out), .in23(registrador32bits_13_out),
    .in24(registrador32bits_20_out), .in25(registrador32bits_26_out), .in26(registrador32bits_26_out),
    .in27(registrador32bits_28_out), .in28(registrador32bits_29_out), .in29(registrador32bits_30_out),
    .in30(registrador32bits_31_out), .in31(registrador32bits_32_out), .out(ViewRegB), .sel(wReg));
  and and_1 (out_8, ~ViewRegA[31], ~ViewRegA[30], ~ViewRegA[29], ~ViewRegA[28], ~ViewRegA[27], ~ViewRegA[26], ~ViewRegA[25], ~ViewRegA[24], ~ViewRegA[23], ~ViewRegA[22], ~ViewRegA[21], ~ViewRegA[20], ~ViewRegA[19], ~ViewRegA[18], ~ViewRegA[17], ~ViewRegA[16], ~ViewRegA[15], ~ViewRegA[14], ~ViewRegA[13], ~ViewRegA[12], ~ViewRegA[11], ~ViewRegA[10], ~ViewRegA[9], ~ViewRegA[8], ~ViewRegA[7], ~ViewRegA[6], ~ViewRegA[5], ~ViewRegA[4], ~ViewRegA[3], ~ViewRegA[2], ~ViewRegA[1], ~ViewRegA[0]);  // AND_Gate
  and and_2 (out_10, ~ViewRegB[31], ~ViewRegB[30], ~ViewRegB[29], ~ViewRegB[28], ~ViewRegB[27], ~ViewRegB[26], ~ViewRegB[25], ~ViewRegB[24], ~ViewRegB[23], ~ViewRegB[22], ~ViewRegB[21], ~ViewRegB[20], ~ViewRegB[19], ~ViewRegB[18], ~ViewRegB[17], ~ViewRegB[16], ~ViewRegB[15], ~ViewRegB[14], ~ViewRegB[13], ~ViewRegB[12], ~ViewRegB[11], ~ViewRegB[10], ~ViewRegB[9], ~ViewRegB[8], ~ViewRegB[7], ~ViewRegB[6], ~ViewRegB[5], ~ViewRegB[4], ~ViewRegB[3], ~ViewRegB[2], ~ViewRegB[1], ~ViewRegB[0]);  // AND_Gate
endmodule

module rascunho (
  input  [3:0] in_1,
  input  in_2,
  input  in_3,
  input  in_4,
  input  in_5,
  input  in_6,
  input  in_7,
  input  in_8,
  input  in_9,
  input  in_10,
  input  in_11,
  input  in_12,
  input  in_13,
  input  in_14,
  input  in_15,
  input  in_16,
  input  in_17,
  input  in_18,
  input  in_19,
  input  in_20,
  input  in_21,
  input  in_22,
  input  in_23,
  input  in_24,
  input  in_25,
  input  in_26,
  input  in_27,
  input  in_28,
  input  in_29,
  input  in_30,
  input  in_31,
  input  in_32,
  input  in_33,
  input  in_34,
  output [3:0] out_35,
  output [3:0] out_36,
  output [3:0] out_37,
  output [3:0] out_38,
  output [3:0] out_39,
  output [3:0] out_40,
  output [3:0] out_41,
  output [3:0] out_42,
  output [3:0] out_43,
  output [3:0] out_44,
  output [3:0] out_45,
  output [3:0] out_46,
  output [3:0] out_47,
  output [3:0] out_48,
  output [3:0] out_49,
  output [3:0] out_50,
  output [3:0] out_51,
  output [3:0] out_52,
  output [3:0] out_53,
  output [3:0] out_54,
  output [3:0] out_55,
  output [3:0] out_56,
  output [3:0] out_57,
  output [3:0] out_58,
  output [3:0] out_59,
  output [3:0] out_60,
  output [3:0] out_61,
  output [3:0] out_62,
  output [3:0] out_63,
  output [3:0] out_64,
  output [3:0] out_65,
  output [3:0] out_66
);

  wire bancoreg4bit_15_p5, bancoreg4bit_16_p2, bancoreg4bit_16_p6, bancoreg4bit_25_p3;

  // BancoReg4bit bancoreg4bit_1: pin names not known; wires that end beside it: in_1, in_2, in_3, out_35
  // BancoReg4bit bancoreg4bit_2: pin names not known; wires that end beside it: in_3, in_1, in_4, in_3, out_36
  // BancoReg4bit bancoreg4bit_3: pin names not known; wires that end beside it: in_3, in_1, in_5, in_3, out_37
  // BancoReg4bit bancoreg4bit_4: pin names not known; wires that end beside it: in_3, in_1, in_6, in_3, out_38
  // BancoReg4bit bancoreg4bit_5: pin names not known; wires that end beside it: in_3, in_1, in_7, in_3, out_39
  // BancoReg4bit bancoreg4bit_6: pin names not known; wires that end beside it: in_3, in_1, in_8, in_3, out_40
  // BancoReg4bit bancoreg4bit_7: pin names not known; wires that end beside it: in_3, in_1, in_9, in_3, out_41
  // BancoReg4bit bancoreg4bit_8: pin names not known; wires that end beside it: in_3, in_1, in_10, in_3, out_42
  // BancoReg4bit bancoreg4bit_9: pin names not known; wires that end beside it: in_3, in_1, in_11, in_3, out_43
  // BancoReg4bit bancoreg4bit_10: pin names not known; wires that end beside it: in_3, in_1, in_12, in_3, out_45
  // BancoReg4bit bancoreg4bit_11: pin names not known; wires that end beside it: in_3, in_1, in_13, in_3, out_46
  // BancoReg4bit bancoreg4bit_12: pin names not known; wires that end beside it: in_3, in_1, in_14, in_3, out_47
  // BancoReg4bit bancoreg4bit_13: pin names not known; wires that end beside it: in_3, in_1, in_15, in_3, out_48
  // BancoReg4bit bancoreg4bit_14: pin names not known; wires that end beside it: in_3, in_1, in_16, in_3, out_49
  // BancoReg4bit bancoreg4bit_15: pin names not known; wires that end beside it: in_3, in_1, in_17, in_3, bancoreg4bit_15_p5
  // BancoReg4bit bancoreg4bit_16: pin names not known; wires that end beside it: in_3, bancoreg4bit_16_p2, in_1, in_18, in_3, bancoreg4bit_16_p6, out_50
  // BancoReg4bit bancoreg4bit_17: pin names not known; wires that end beside it: in_3, bancoreg4bit_16_p2, in_1, in_18, in_3, bancoreg4bit_16_p6, out_50
  // BancoReg4bit bancoreg4bit_18: pin names not known; wires that end beside it: in_3, in_1, in_19, in_3, out_51
  // BancoReg4bit bancoreg4bit_19: pin names not known; wires that end beside it: in_3, in_1, in_20, in_3, out_52
  // BancoReg4bit bancoreg4bit_20: pin names not known; wires that end beside it: in_3, in_1, in_21, in_3, out_53
  // BancoReg4bit bancoreg4bit_21: pin names not known; wires that end beside it: in_3, in_1, in_22, in_3, out_54
  // BancoReg4bit bancoreg4bit_22: pin names not known; wires that end beside it: in_3, in_1, in_23, in_3, out_55
  // BancoReg4bit bancoreg4bit_23: pin names not known; wires that end beside it: in_3, in_1, in_24, in_3, out_56
  // BancoReg4bit bancoreg4bit_24: pin names not known; wires that end beside it: in_3, in_1, in_25, in_3, out_57
  // BancoReg4bit bancoreg4bit_25: pin names not known; wires that end beside it: in_3, in_1, bancoreg4bit_25_p3, in_3, out_58
  // BancoReg4bit bancoreg4bit_26: pin names not known; wires that end beside it: in_3, in_1, in_26, in_3, out_59
  // BancoReg4bit bancoreg4bit_27: pin names not known; wires that end beside it: in_3, in_1, in_28, in_3, out_60
  // BancoReg4bit bancoreg4bit_28: pin names not known; wires that end beside it: in_3, in_1, in_29, in_3, out_61
  // BancoReg4bit bancoreg4bit_29: pin names not known; wires that end beside it: in_3, in_1, in_30, in_3, out_62
  // BancoReg4bit bancoreg4bit_30: pin names not known; wires that end beside it: in_3, in_1, in_31, in_3, out_63
  // BancoReg4bit bancoreg4bit_31: pin names not known; wires that end beside it: in_3, in_1, in_32, in_3, out_64
  // BancoReg4bit bancoreg4bit_32: pin names not known; wires that end beside it: in_3, in_1, in_33, in_3, out_65
  // BancoReg4bit bancoreg4bit_33: pin names not known; wires that end beside it: in_3, in_1, in_34, in_3, out_66

  assign in_27 = in_26;
  assign out_44 = out_43;
endmodule

module SelBancoReg32bits (
  input  [31:0] Data,
  input  Reset,
  input  CLK,
  input  in_4,
  input  [4:0] Wreg,
  input  [4:0] RegA,
  input  [4:0] RegB,
  output Zero_A,
  output Zero_B,
  output [31:0] ViewA,
  output [31:0] ViewB,
  output Zero_A_2,
  output Zero_B_2
);

  wire demultiplexer_1_out0, demultiplexer_1_out1;
  wire [31:0] bancoreg32bits_1_viewrega, bancoreg32bits_1_viewregb, bancoreg32bits_2_viewrega,
       bancoreg32bits_2_viewregb;

  Demultiplexer #(.enable("false")) demultiplexer_1 (
    .out0(demultiplexer_1_out0), .out1(demultiplexer_1_out1), .in(CLK), .sel(in_4));
  BancoReg32bits bancoreg32bits_1 (
    .Reset(Reset), .CLK(demultiplexer_1_out0), .Data(Data), .in_5(Wreg), .in_3(RegA), .wReg(RegB),
    .ViewRegA(bancoreg32bits_1_viewrega), .ViewRegB(bancoreg32bits_1_viewregb), .out_10(Zero_B),
    .out_8(Zero_A));
  BancoReg32bits bancoreg32bits_2 (
    .Reset(Reset), .CLK(demultiplexer_1_out1), .Data(Data), .in_5(Wreg), .in_3(RegA), .wReg(RegB),
    .ViewRegA(bancoreg32bits_2_viewrega), .ViewRegB(bancoreg32bits_2_viewregb), .out_10(Zero_B_2),
    .out_8(Zero_A_2));
  Multiplexer #(.width(32), .enable("false")) multiplexer_1 (
    .in0(bancoreg32bits_1_viewregb), .in1(bancoreg32bits_2_viewregb), .out(ViewB), .sel(in_4));
  Multiplexer #(.width(32), .enable("false")) multiplexer_2 (
    .in0(bancoreg32bits_1_viewrega), .in1(bancoreg32bits_2_viewrega), .out(ViewA), .sel(in_4));
endmodule
