// Logisim project ConnectionData4bits.circ as structural Verilog: 5 circuits, main circuit main
module main (
  input  in_1,
  input  in_2,
  input  i,
  input  [10:0] Instruction,
  input  [3:0] Imm,
  output out_6,
  output [15:0] out_7
);

  wire not_1_out;
  wire [3:0] banco8reg4bits_1_viewrega, banco8reg4bits_1_viewregb, multiplexer_1_out, ula_1_s;
  wire [7:0] adder_1_out, PC_q;

  Adder adder_1 (.a(PC_q), .b(8'h1), .out(adder_1_out), .cin(1'b0));  // open: cout
  Register PC (.D(adder_1_out), .Q(PC_q), .clk(not_1_out), .clr(in_2));  // open: en
  not not_1 (not_1_out, in_1);
  RAM #(.dataWidth(16)) ram_1 (.addr(PC_q), .data(out_7));  // open: sel, clk, ld, clr
  Banco8Reg4bits banco8reg4bits_1 (
    .CLK(in_1), .Data(ula_1_s), .WReg(out_7[13:11]), .Reset(in_2), .RegA(out_7[10:8]), .RegB(out_7[7:5]),
    .ViewRegA(banco8reg4bits_1_viewrega), .ViewRegB(banco8reg4bits_1_viewregb));
  ULA ula_1 (.A(banco8reg4bits_1_viewrega), .B(multiplexer_1_out), .Zero(out_6), .S(ula_1_s), .OpCode(out_7[15:14]));
  Multiplexer #(.width(4), .enable("false")) multiplexer_1 (
    .in0(banco8reg4bits_1_viewregb), .in1(out_7[4:1]), .out(multiplexer_1_out), .sel(out_7[0]));

  // Notes on the sheet:
  //   1000 1000 0000 0111
  //   1001 0000 0000 1111
  //   1001 1001 0100 0000
endmodule

module Registrador4bits (
  input  [3:0] DataIN,
  input  Save,
  input  Reset,
  output [3:0] DataOUT
);

  D_Flip_Flop d_ff_1 (.clk(Save), .D(DataIN[3]), .Q(DataOUT[3]), .reset(Reset));  // open: Qn, preset, en
  D_Flip_Flop d_ff_2 (.clk(Save), .D(DataIN[2]), .Q(DataOUT[2]), .reset(Reset));  // open: Qn, preset, en
  D_Flip_Flop d_ff_3 (.clk(Save), .D(DataIN[1]), .Q(DataOUT[1]), .reset(Reset));  // open: Qn, preset, en
  D_Flip_Flop d_ff_4 (.clk(Save), .D(DataIN[0]), .Q(DataOUT[0]), .reset(Reset));  // open: Qn, preset, en
endmodule

module Banco8Reg4bits (
  input  [3:0] Data,
  input  Reset,
  input  [2:0] RegA,
  input  CLK,
  input  [2:0] WReg,
  input  [2:0] RegB,
  output [3:0] ViewRegA,
  output [3:0] ViewRegB
);

  wire demultiplexer_1_out0, demultiplexer_1_out1, demultiplexer_1_out2, demultiplexer_1_out3,
       demultiplexer_1_out4, demultiplexer_1_out5, demultiplexer_1_out6, demultiplexer_1_out7;
  wire [3:0] registrador4bits_1_dataout, registrador4bits_2_dataout, registrador4bits_3_dataout,
       registrador4bits_4_dataout, registrador4bits_5_dataout, registrador4bits_6_dataout,
       registrador4bits_7_dataout, registrador4bits_8_dataout;

  Demultiplexer #(.select(3), .enable("false")) demultiplexer_1 (
    .out0(demultiplexer_1_out0), .out1(demultiplexer_1_out1), .out2(demultiplexer_1_out2),
    .out3(demultiplexer_1_out3), .out4(demultiplexer_1_out4), .out5(demultiplexer_1_out5),
    .out6(demultiplexer_1_out6), .out7(demultiplexer_1_out7), .in(CLK), .sel(WReg));
  Registrador4bits registrador4bits_1 (
    .DataIN(Data), .Save(demultiplexer_1_out0), .Reset(Reset), .DataOUT(registrador4bits_1_dataout));
  Registrador4bits registrador4bits_2 (
    .DataIN(Data), .Save(demultiplexer_1_out1), .Reset(Reset), .DataOUT(registrador4bits_2_dataout));
  Registrador4bits registrador4bits_3 (
    .DataIN(Data), .Save(demultiplexer_1_out2), .Reset(Reset), .DataOUT(registrador4bits_3_dataout));
  Registrador4bits registrador4bits_4 (
    .DataIN(Data), .Save(demultiplexer_1_out3), .Reset(Reset), .DataOUT(registrador4bits_4_dataout));
  Registrador4bits registrador4bits_5 (
    .DataIN(Data), .Save(demultiplexer_1_out4), .Reset(Reset), .DataOUT(registrador4bits_5_dataout));
  Registrador4bits registrador4bits_6 (
    .DataIN(Data), .Save(demultiplexer_1_out5), .Reset(Reset), .DataOUT(registrador4bits_6_dataout));
  Registrador4bits registrador4bits_7 (
    .DataIN(Data), .Save(demultiplexer_1_out6), .Reset(Reset), .DataOUT(registrador4bits_7_dataout));
  Registrador4bits registrador4bits_8 (
    .DataIN(Data), .Save(demultiplexer_1_out7), .Reset(Reset), .DataOUT(registrador4bits_8_dataout));
  Multiplexer #(.select(3), .width(4), .enable("false")) multiplexer_1 (
    .in0(registrador4bits_1_dataout), .in1(registrador4bits_2_dataout), .in2(registrador4bits_3_dataout),
    .in3(registrador4bits_4_dataout), .in4(registrador4bits_5_dataout), .in5(registrador4bits_6_dataout),
    .in6(registrador4bits_7_dataout), .in7(registrador4bits_8_dataout), .out(ViewRegA), .sel(RegA));
  Multiplexer #(.select(3), .width(4), .enable("false")) multiplexer_2 (
    .in0(registrador4bits_1_dataout), .in1(registrador4bits_2_dataout), .in2(registrador4bits_3_dataout),
    .in3(registrador4bits_4_dataout), .in4(registrador4bits_5_dataout), .in5(registrador4bits_6_dataout),
    .in6(registrador4bits_7_dataout), .in7(registrador4bits_8_dataout), .out(ViewRegB), .sel(RegB));
endmodule

module ULA (
  input  [3:0] A,
  input  [3:0] B,
  input  [1:0] OpCode,
  output Zero,
  output [3:0] S
);

  wire [3:0] adder_1_out, and_1_out, or_1_out;

  assign or_1_out = A | B;  // OR_Gate or_1, 4 bits wide
  assign and_1_out = A & B;  // AND_Gate and_1, 4 bits wide
  Adder #(.width(4)) adder_1 (.a(A), .b(B), .out(adder_1_out), .cin(1'b0));  // open: cout
  Multiplexer #(.select(2), .width(4), .enable("false")) multiplexer_1 (
    .in0(or_1_out), .in1(and_1_out), .in2(adder_1_out), .in3(B), .out(S), .sel(OpCode));
  nor nor_1 (Zero, S[0], S[1], S[3], S[2]);
endmodule

module ext (
  input  [10:0] in_1,
  output [31:0] out_2
);


  assign out_2 = {{22{in_1[10]}}, in_1[9:0]};
endmodule
