// Logisim project ConnectionRegaAndUla.circ as structural Verilog: 4 circuits, main circuit main
module main (
  input  in_1,
  input  in_2,
  output out_3,
  output out_4,
  output [31:0] out_5,
  output out_6,
  output [31:0] out_7
);

  wire not_1_out;
  wire [7:0] adder_1_out, PC_q;
  wire [31:0] bancoreg32bits_1_viewrega, bancoreg32bits_1_viewregb, multiplexer_1_out;

  Adder adder_1 (.a(PC_q), .b(8'h1), .out(adder_1_out), .cin(1'b0));  // open: cout
  Register PC (.D(adder_1_out), .Q(PC_q), .clk(not_1_out), .clr(in_1));  // open: en
  not not_1 (not_1_out, in_1);
  RAM #(.dataWidth(32)) ram_1 (.addr(PC_q), .data(out_7));  // open: sel, clk, ld, clr
  BancoReg32bits bancoreg32bits_1 (
    .Reset(in_1), .CLK(in_1), .ViewRegA(bancoreg32bits_1_viewrega), .out_8(out_3),
    .ViewRegB(bancoreg32bits_1_viewregb), .out_10(out_4), .Data(out_5), .Wreg(out_7[26:22]),
    .regA(out_7[21:17]), .RegB(out_7[16:12]));
  Multiplexer #(.width(32), .enable("false")) multiplexer_1 (
    .in0(bancoreg32bits_1_viewregb), .in1({{22{out_7[11]}}, out_7[10:1]}), .out(multiplexer_1_out),
    .sel(out_7[0]));
  Ulafinal ulafinal_1 (
    .A(bancoreg32bits_1_viewrega), .B(multiplexer_1_out), .Out(out_5), .ULA_OpCode(out_7[31:27]),
    .out_4(out_6));  // open: out_5

  assign in_2 = in_1;

  // Notes on the sheet:
  //   00000 - AND
  //   00001 - OR
  //   00011 - XOR
  //   00100 - SLL A
  //   00101 - SLL B
  //   01101 - NOR
  //   10010 - A
  //   10011 - B
  //   00010 - SOMADOR
  //   00110 - SRL A
  //   00111 - SRL B
  //   01000 - SLA A
  //   01001 - SLA B
  //   01010 - SRA A
  //   01011 - SRA B
  //   01100 - NAND
  //   01110 - XNOR
  //   01111 - NOT A
  //   10000 - NOT B
  //   10001 - NOT A+B
  //   11111 - ZERO
endmodule

module Reg32bits (
  input  [31:0] INPUT,
  input  SAVE,
  input  Reset,
  output [31:0] OUT
);

  D_Flip_Flop d_ff_1 (.clk(SAVE), .D(INPUT[31]), .Q(OUT[31]), .reset(Reset));  // open: Qn, preset, en
  D_Flip_Flop d_ff_2 (.D(INPUT[30]), .Q(OUT[30]), .reset(Reset));  // open: clk, Qn, preset, en
  D_Flip_Flop d_ff_3 (.clk(SAVE), .D(INPUT[29]), .Q(OUT[29]), .reset(Reset));  // open: Qn, preset, en
  D_Flip_Flop d_ff_4 (.clk(SAVE), .D(INPUT[28]), .Q(OUT[28]), .reset(Reset));  // open: Qn, preset, en
  D_Flip_Flop d_ff_5 (.clk(SAVE), .D(INPUT[27]), .Q(OUT[27]), .reset(Reset));  // open: Qn, preset, en
  D_Flip_Flop d_ff_6 (.clk(SAVE), .D(INPUT[26]), .Q(OUT[26]), .reset(Reset));  // open: Qn, preset, en
  D_Flip_Flop d_ff_7 (.clk(SAVE), .D(INPUT[25]), .Q(OUT[25]), .reset(Reset));  // open: Qn, preset, en
  D_Flip_Flop d_ff_8 (.clk(SAVE), .D(INPUT[24]), .Q(OUT[24]), .reset(Reset));  // open: Qn, preset, en
  D_Flip_Flop d_ff_9 (.clk(SAVE), .D(INPUT[23]), .Q(OUT[23]), .reset(Reset));  // open: Qn, preset, en
  D_Flip_Flop d_ff_10 (.clk(SAVE), .D(INPUT[22]), .Q(OUT[22]), .reset(Reset));  // open: Qn, preset, en
  D_Flip_Flop d_ff_11 (.clk(SAVE), .D(INPUT[21]), .Q(OUT[21]), .reset(Reset));  // open: Qn, preset, en
  D_Flip_Flop d_ff_12 (.clk(SAVE), .D(INPUT[20]), .Q(OUT[20]), .reset(Reset));  // open: Qn, preset, en
  D_Flip_Flop d_ff_13 (.clk(SAVE), .D(INPUT[19]), .Q(OUT[19]), .reset(Reset));  // open: Qn, preset, en
  D_Flip_Flop d_ff_14 (.clk(SAVE), .D(INPUT[18]), .Q(OUT[18]), .reset(Reset));  // open: Qn, preset, en
  D_Flip_Flop d_ff_15 (.clk(SAVE), .D(INPUT[17]), .Q(OUT[17]), .reset(Reset));  // open: Qn, preset, en
  D_Flip_Flop d_ff_16 (.clk(SAVE), .D(INPUT[16]), .Q(OUT[16]), .reset(Reset));  // open: Qn, preset, en
  D_Flip_Flop d_ff_17 (.clk(SAVE), .D(INPUT[15]), .Q(OUT[15]), .reset(Reset));  // open: Qn, preset, en
  D_Flip_Flop d_ff_18 (.clk(SAVE), .D(INPUT[14]), .Q(OUT[14]), .reset(Reset));  // open: Qn, preset, en
  D_Flip_Flop d_ff_19 (.clk(SAVE), .D(INPUT[13]), .Q(OUT[13]), .reset(Reset));  // open: Qn, preset, en
  D_Flip_Flop d_ff_20 (.clk(SAVE), .D(INPUT[12]), .Q(OUT[12]), .reset(Reset));  // open: Qn, preset, en
  D_Flip_Flop d_ff_21 (.clk(SAVE), .D(INPUT[11]), .Q(OUT[11]), .reset(Reset));  // open: Qn, preset, en
  D_Flip_Flop d_ff_22 (.clk(SAVE), .D(INPUT[10]), .Q(OUT[10]), .reset(Reset));  // open: Qn, preset, en
  D_Flip_Flop d_ff_23 (.clk(SAVE), .D(INPUT[9]), .Q(OUT[9]), .reset(Reset));  // open: Qn, preset, en
  D_Flip_Flop d_ff_24 (.clk(SAVE), .D(INPUT[8]), .Q(OUT[8]), .reset(Reset));  // open: Qn, preset, en
  D_Flip_Flop d_ff_25 (.clk(SAVE), .D(INPUT[7]), .Q(OUT[7]), .reset(Reset));  // open: Qn, preset, en
  D_Flip_Flop d_ff_26 (.clk(SAVE), .D(INPUT[6]), .Q(OUT[6]), .reset(Reset));  // open: Qn, preset, en
  D_Flip_Flop d_ff_27 (.clk(SAVE), .D(INPUT[5]), .Q(OUT[5]), .reset(Reset));  // open: Qn, preset, en
  D_Flip_Flop d_ff_28 (.clk(SAVE), .D(INPUT[4]), .Q(OUT[4]), .reset(Reset));  // open: Qn, preset, en
  D_Flip_Flop d_ff_29 (.clk(SAVE), .D(INPUT[3]), .Q(OUT[3]), .reset(Reset));  // open: Qn, preset, en
  D_Flip_Flop d_ff_30 (.clk(SAVE), .D(INPUT[2]), .Q(OUT[2]), .reset(Reset));  // open: Qn, preset, en
  D_Flip_Flop d_ff_31 (.clk(SAVE), .D(INPUT[1]), .Q(OUT[1]), .reset(Reset));  // open: Qn, preset, en
  D_Flip_Flop d_ff_32 (.clk(SAVE), .D(INPUT[0]), .Q(OUT[0]), .reset(Reset));  // open: Qn, preset, en
endmodule

module BancoReg32bits (
  input  [31:0] Data,
  input  Reset,
  input  [4:0] regA,
  input  CLK,
  input  [4:0] Wreg,
  input  [4:0] RegB,
  output [31:0] ViewRegA,
  output out_8,
  output [31:0] ViewRegB,
  output out_10
);

  wire demultiplexer_1_out0, demultiplexer_1_out1, demultiplexer_1_out2, demultiplexer_1_out3,
       demultiplexer_1_out4, demultiplexer_1_out5, demultiplexer_1_out6, demultiplexer_1_out7,
       demultiplexer_1_out8, demultiplexer_1_out9, demultiplexer_1_out10, demultiplexer_1_out11,
       demultiplexer_1_out12, demultiplexer_1_out13, demultiplexer_1_out14, demultiplexer_1_out15,
       demultiplexer_1_out16, demultiplexer_1_out17, demultiplexer_1_out18, demultiplexer_1_out19,
       demultiplexer_1_out20, demultiplexer_1_out21, demultiplexer_1_out22, demultiplexer_1_out23,
       demultiplexer_1_out24, demultiplexer_1_out25, demultiplexer_1_out26, demultiplexer_1_out27,
       demultiplexer_1_out28, demultiplexer_1_out29, demultiplexer_1_out30, demultiplexer_1_out31;
  wire [31:0] reg32bits_1_out, reg32bits_2_out, reg32bits_3_out, reg32bits_4_out, reg32bits_5_out,
       reg32bits_6_out, reg32bits_7_out, reg32bits_8_out, reg32bits_9_out, reg32bits_10_out,
       reg32bits_11_out, reg32bits_12_out, reg32bits_13_out, reg32bits_14_out, reg32bits_15_out,
       reg32bits_16_out, reg32bits_17_out, reg32bits_18_out, reg32bits_19_out, reg32bits_20_out,
       reg32bits_21_out, reg32bits_22_out, reg32bits_26_out, reg32bits_28_out, reg32bits_29_out,
       reg32bits_30_out, reg32bits_31_out, reg32bits_32_out;

  Demultiplexer #(.select(5), .enable("false")) demultiplexer_1 (
    .out0(demultiplexer_1_out0), .out1(demultiplexer_1_out1), .out2(demultiplexer_1_out2),
    .out3(demultiplexer_1_out3), .out4(demultiplexer_1_out4), .out5(demultiplexer_1_out5),
    .out6(demultiplexer_1_out6), .out7(demultiplexer_1_out7), .out8(demultiplexer_1_out8),
    .out9(demultiplexer_1_out9), .out10(demultiplexer_1_out10), .out11(demultiplexer_1_out11),
    .out12(demultiplexer_1_out12), .out13(demultiplexer_1_out13), .out14(demultiplexer_1_out14),
    .out15(demultiplexer_1_out15), .out16(demultiplexer_1_out16), .out17(demultiplexer_1_out17),
    .out18(demultiplexer_1_out18), .out19(demultiplexer_1_out19), .out20(demultiplexer_1_out20),
    .out21(demultiplexer_1_out21), .out22(demultiplexer_1_out22), .out23(demultiplexer_1_out23),
    .out24(demultiplexer_1_out24), .out25(demultiplexer_1_out25), .out26(demultiplexer_1_out26),
    .out27(demultiplexer_1_out27), .out28(demultiplexer_1_out28), .out29(demultiplexer_1_out29),
    .out30(demultiplexer_1_out30), .out31(demultiplexer_1_out31), .in(CLK), .sel(Wreg));
  Reg32bits reg32bits_1 (.SAVE(demultiplexer_1_out0), .Reset(Reset), .INPUT(Data), .OUT(reg32bits_1_out));
  Reg32bits reg32bits_2 (.SAVE(demultiplexer_1_out1), .Reset(Reset), .INPUT(Data), .OUT(reg32bits_2_out));
  Reg32bits reg32bits_3 (.SAVE(demultiplexer_1_out2), .Reset(Reset), .INPUT(Data), .OUT(reg32bits_3_out));
  Reg32bits reg32bits_4 (.SAVE(demultiplexer_1_out3), .Reset(Reset), .INPUT(Data), .OUT(reg32bits_4_out));
  Reg32bits reg32bits_5 (.SAVE(demultiplexer_1_out4), .Reset(Reset), .INPUT(Data), .OUT(reg32bits_5_out));
  Reg32bits reg32bits_6 (.SAVE(demultiplexer_1_out5), .Reset(Reset), .INPUT(Data), .OUT(reg32bits_6_out));
  Reg32bits reg32bits_7 (.SAVE(demultiplexer_1_out6), .Reset(Reset), .INPUT(Data), .OUT(reg32bits_7_out));
  Reg32bits reg32bits_8 (.SAVE(demultiplexer_1_out7), .Reset(Reset), .INPUT(Data), .OUT(reg32bits_8_out));
  Reg32bits reg32bits_9 (.SAVE(demultiplexer_1_out8), .Reset(Reset), .INPUT(Data), .OUT(reg32bits_9_out));
  Reg32bits reg32bits_10 (.SAVE(demultiplexer_1_out9), .Reset(Reset), .INPUT(Data), .OUT(reg32bits_10_out));
  Reg32bits reg32bits_11 (.SAVE(demultiplexer_1_out10), .Reset(Reset), .INPUT(Data), .OUT(reg32bits_11_out));
  Reg32bits reg32bits_12 (.SAVE(demultiplexer_1_out11), .Reset(Reset), .INPUT(Data), .OUT(reg32bits_12_out));
  Reg32bits reg32bits_13 (.SAVE(demultiplexer_1_out12), .Reset(Reset), .INPUT(Data), .OUT(reg32bits_13_out));
  Reg32bits reg32bits_14 (.SAVE(demultiplexer_1_out13), .Reset(Reset), .INPUT(Data), .OUT(reg32bits_14_out));
  Reg32bits reg32bits_15 (.SAVE(demultiplexer_1_out14), .Reset(Reset), .INPUT(Data), .OUT(reg32bits_15_out));
  Reg32bits reg32bits_16 (.SAVE(demultiplexer_1_out15), .Reset(Reset), .INPUT(Data), .OUT(reg32bits_16_out));
  Reg32bits reg32bits_17 (.SAVE(demultiplexer_1_out16), .Reset(Reset), .INPUT(Data), .OUT(reg32bits_17_out));
  Reg32bits reg32bits_18 (.SAVE(demultiplexer_1_out17), .Reset(Reset), .INPUT(Data), .OUT(reg32bits_18_out));
  Reg32bits reg32bits_19 (.SAVE(demultiplexer_1_out18), .Reset(Reset), .INPUT(Data), .OUT(reg32bits_19_out));
  Reg32bits reg32bits_20 (.SAVE(demultiplexer_1_out19), .Reset(Reset), .INPUT(Data), .OUT(reg32bits_20_out));
  Reg32bits reg32bits_21 (.SAVE(demultiplexer_1_out20), .Reset(Reset), .INPUT(Data), .OUT(reg32bits_21_out));
  Reg32bits reg32bits_22 (.SAVE(demultiplexer_1_out21), .Reset(Reset), .INPUT(Data), .OUT(reg32bits_22_out));
  Reg32bits reg32bits_23 (.SAVE(demultiplexer_1_out22), .Reset(Reset), .INPUT(Data), .OUT(reg32bits_6_out));
  Reg32bits reg32bits_24 (.SAVE(demultiplexer_1_out23), .Reset(Reset), .INPUT(Data), .OUT(reg32bits_13_out));
  Reg32bits reg32bits_25 (.SAVE(demultiplexer_1_out24), .Reset(Reset), .INPUT(Data), .OUT(reg32bits_20_out));
  Reg32bits reg32bits_26 (.SAVE(demultiplexer_1_out25), .Reset(Reset), .INPUT(Data), .OUT(reg32bits_26_out));
  Reg32bits reg32bits_27 (.SAVE(demultiplexer_1_out26), .Reset(Reset), .INPUT(Data), .OUT(reg32bits_26_out));
  Reg32bits reg32bits_28 (.SAVE(demultiplexer_1_out27), .Reset(Reset), .INPUT(Data), .OUT(reg32bits_28_out));
  Reg32bits reg32bits_29 (.SAVE(demultiplexer_1_out28), .Reset(Reset), .INPUT(Data), .OUT(reg32bits_29_out));
  Reg32bits reg32bits_30 (.SAVE(demultiplexer_1_out29), .Reset(Reset), .INPUT(Data), .OUT(reg32bits_30_out));
  Reg32bits reg32bits_31 (.SAVE(demultiplexer_1_out30), .Reset(Reset), .INPUT(Data), .OUT(reg32bits_31_out));
  Reg32bits reg32bits_32 (.SAVE(demultiplexer_1_out31), .Reset(Reset), .INPUT(Data), .OUT(reg32bits_32_out));
  Multiplexer #(.select(5), .width(32), .enable("false")) multiplexer_1 (
    .in0(reg32bits_1_out), .in1(reg32bits_2_out), .in2(reg32bits_3_out), .in3(reg32bits_4_out),
    .in4(reg32bits_5_out), .in5(reg32bits_6_out), .in6(reg32bits_7_out), .in7(reg32bits_8_out),
    .in8(reg32bits_9_out), .in9(reg32bits_10_out), .in10(reg32bits_11_out), .in11(reg32bits_12_out),
    .in12(reg32bits_13_out), .in13(reg32bits_14_out), .in14(reg32bits_15_out), .in15(reg32bits_16_out),
    .in16(reg32bits_17_out), .in17(reg32bits_18_out), .in18(reg32bits_19_out), .in19(reg32bits_20_out),
    .in20(reg32bits_21_out), .in21(reg32bits_22_out), .in22(reg32bits_6_out), .in23(reg32bits_13_out),
    .in24(reg32bits_20_out), .in25(reg32bits_26_out), .in26(reg32bits_26_out), .in27(reg32bits_28_out),
    .in28(reg32bits_29_out), .in29(reg32bits_30_out), .in30(reg32bits_31_out), .in31(reg32bits_32_out),
    .out(ViewRegA), .sel(regA));
  Multiplexer #(.select(5), .width(32), .enable("false")) multiplexer_2 (
    .in0(reg32bits_1_out), .in1(reg32bits_2_out), .in2(reg32bits_3_out), .in3(reg32bits_4_out),
    .in4(reg32bits_5_out), .in5(reg32bits_6_out), .in6(reg32bits_7_out), .in7(reg32bits_8_out),
    .in8(reg32bits_9_out), .in9(reg32bits_10_out), .in10(reg32bits_11_out), .in11(reg32bits_12_out),
    .in12(reg32bits_13_out), .in13(reg32bits_14_out), .in14(reg32bits_15_out), .in15(reg32bits_16_out),
    .in16(reg32bits_17_out), .in17(reg32bits_18_out), .in18(reg32bits_19_out), .in19(reg32bits_20_out),
    .in20(reg32bits_21_out), .in21(reg32bits_22_out), .in22(reg32bits_6_out), .in23(reg32bits_13_out),
    .in24(reg32bits_20_out), .in25(reg32bits_26_out), .in26(reg32bits_26_out), .in27(reg32bits_28_out),
    .in28(reg32bits_29_out), .in29(reg32bits_30_out), .in30(reg32bits_31_out), .in31(reg32bits_32_out),
    .out(ViewRegB), .sel(RegB));
  and and_1 (out_8, ~ViewRegA[31], ~ViewRegA[30], ~ViewRegA[29], ~ViewRegA[28], ~ViewRegA[27], ~ViewRegA[26], ~ViewRegA[25], ~ViewRegA[24], ~ViewRegA[23], ~ViewRegA[22], ~ViewRegA[21], ~ViewRegA[20], ~ViewRegA[19], ~ViewRegA[18], ~ViewRegA[17], ~ViewRegA[16], ~ViewRegA[15], ~ViewRegA[14], ~ViewRegA[13], ~ViewRegA[12], ~ViewRegA[11], ~ViewRegA[10], ~ViewRegA[9], ~ViewRegA[8], ~ViewRegA[7], ~ViewRegA[6], ~ViewRegA[5], ~ViewRegA[4], ~ViewRegA[3], ~ViewRegA[2], ~ViewRegA[1], ~ViewRegA[0]);  // AND_Gate
  and and_2 (out_10, ~ViewRegB[31], ~ViewRegB[30], ~ViewRegB[29], ~ViewRegB[28], ~ViewRegB[27], ~ViewRegB[26], ~ViewRegB[25], ~ViewRegB[24], ~ViewRegB[23], ~ViewRegB[22], ~ViewRegB[21], ~ViewRegB[20], ~ViewRegB[19], ~ViewRegB[18], ~ViewRegB[17], ~ViewRegB[16], ~ViewRegB[15], ~ViewRegB[14], ~ViewRegB[13], ~ViewRegB[12], ~ViewRegB[11], ~ViewRegB[10], ~ViewRegB[9], ~ViewRegB[8], ~ViewRegB[7], ~ViewRegB[6], ~ViewRegB[5], ~ViewRegB[4], ~ViewRegB[3], ~ViewRegB[2], ~ViewRegB[1], ~ViewRegB[0]);  // AND_Gate
endmodule

module rascunho (
  input  [9:0] in_1,
  output [31:0] out_2
);


  assign out_2 = {{23{in_1[9]}}, in_1[8:0]};
endmodule
