// Logisim project Mux.circ as structural Verilog: 6 circuits, main circuit Mux2:1
module Mux2_1 (
  input  A,
  input  B,
  input  Sel,
  output out_4
);

  wire and_1_out, and_2_out;

  and and_1 (and_1_out, A, ~Sel);  // AND_Gate
  and and_2 (and_2_out, B, Sel);
  or or_1 (out_4, and_1_out, and_2_out);

  // Notes on the sheet:
  //   A(1) e S(0) -> A
  //   B(1) e S(1) -> B
endmodule

module Mux4_1 (
  input  A,
  input  B,
  input  C,
  input  D,
  input  SEL_0,
  input  SEL_1,
  output out_7
);

  wire mux2_1_1_out_4, mux2_1_2_out_4;

  Mux2_1 mux2_1_1 (.A(C), .B(D), .Sel(SEL_1), .out_4(mux2_1_1_out_4));
  Mux2_1 mux2_1_2 (.A(A), .B(B), .Sel(SEL_1), .out_4(mux2_1_2_out_4));
  Mux2_1 mux2_1_3 (.A(mux2_1_2_out_4), .B(mux2_1_1_out_4), .Sel(SEL_0), .out_4(out_7));

  // Notes on the sheet:
  //   00 = A
  //   01 = B
  //   10 = C
  //   11 = D
  //   0 = DESLIGADO
  //   1= LIGADO
endmodule

module Mux8_1 (
  input  A,
  input  B,
  input  C,
  input  D,
  input  E,
  input  F,
  input  G,
  input  H,
  input  SEL_0,
  input  SEL_1,
  input  SEL_2,
  output out_12
);

  wire mux4_1_1_out_7, mux4_1_2_out_7;

  Mux4_1 mux4_1_1 (.A(E), .B(F), .C(G), .D(H), .SEL_0(SEL_1), .SEL_1(SEL_2), .out_7(mux4_1_1_out_7));
  Mux4_1 mux4_1_2 (.A(A), .B(B), .C(C), .D(D), .SEL_0(SEL_1), .SEL_1(SEL_2), .out_7(mux4_1_2_out_7));
  Mux2_1 mux2_1_1 (.A(mux4_1_2_out_7), .B(mux4_1_1_out_7), .Sel(SEL_0), .out_4(out_12));
endmodule

module Mux16_1 (
  input  A,
  input  B,
  input  C,
  input  D,
  input  E,
  input  F,
  input  G,
  input  H,
  input  I,
  input  J,
  input  K,
  input  L,
  input  M,
  input  N,
  input  O,
  input  P,
  input  S0,
  input  S1,
  input  S2,
  input  S3,
  output out_21
);

  wire mux8_1_1_out_12, mux8_1_2_out_12;

  Mux8_1 mux8_1_1 (
    .A(I), .B(J), .C(K), .D(L), .E(M), .F(N), .G(O), .H(P), .SEL_0(S1), .SEL_1(S2), .SEL_2(S3),
    .out_12(mux8_1_1_out_12));
  Mux8_1 mux8_1_2 (
    .A(A), .B(B), .C(C), .D(D), .E(E), .F(F), .G(G), .H(H), .SEL_0(S1), .SEL_1(S2), .SEL_2(S3),
    .out_12(mux8_1_2_out_12));
  Mux2_1 mux2_1_1 (.A(mux8_1_2_out_12), .B(mux8_1_1_out_12), .Sel(S0), .out_4(out_21));
endmodule

module Mux32_1 (
  input  C0,
  input  C1,
  input  C2,
  input  C3,
  input  C4,
  input  C5,
  input  C6,
  input  C7,
  input  C8,
  input  C9,
  input  C10,
  input  C11,
  input  C12,
  input  C13,
  input  C14,
  input  C15,
  input  C16,
  input  C17,
  input  C18,
  input  C19,
  input  C20,
  input  C21,
  input  C22,
  input  C23,
  input  C24,
  input  C25,
  input  C26,
  input  C27,
  input  C28,
  input  C29,
  input  C30,
  input  C31,
  input  S0,
  input  S1,
  input  S2,
  input  S3,
  input  S4,
  output out_38
);

  wire mux16_1_1_out_21, mux16_1_2_out_21;

  Mux16_1 mux16_1_1 (
    .A(C16), .B(C17), .C(C18), .D(C19), .E(C20), .F(C21), .G(C22), .H(C23), .I(C24), .J(C25), .K(C26),
    .L(C27), .M(C28), .N(C29), .O(C30), .P(C31), .S0(S1), .S1(S2), .S2(S3), .S3(S4), .out_21(mux16_1_1_out_21));
  Mux16_1 mux16_1_2 (
    .A(C0), .B(C1), .C(C2), .D(C3), .E(C4), .F(C5), .G(C6), .H(C7), .I(C8), .J(C9), .K(C10), .L(C11),
    .M(C12), .N(C13), .O(C14), .P(C15), .S0(S1), .S1(S2), .S2(S3), .S3(S4), .out_21(mux16_1_2_out_21));
  Mux2_1 mux2_1_1 (.A(mux16_1_2_out_21), .B(mux16_1_1_out_21), .Sel(S0), .out_4(out_38));
endmodule

module Mux64_1 (
  input  C0,
  input  C1,
  input  C2,
  input  C3,
  input  C4,
  input  C5,
  input  C6,
  input  C7,
  input  C8,
  input  C9,
  input  C10,
  input  C11,
  input  C12,
  input  C13,
  input  C14,
  input  C15,
  input  C16,
  input  C17,
  input  C18,
  input  C19,
  input  C20,
  input  C21,
  input  C22,
  input  C23,
  input  C24,
  input  C25,
  input  C26,
  input  C27,
  input  C28,
  input  C29,
  input  C30,
  input  C31,
  input  C32,
  input  C33,
  input  C34,
  input  C35,
  input  C36,
  input  C37,
  input  C38,
  input  C39,
  input  C40,
  input  C41,
  input  C42,
  input  C43,
  input  C44,
  input  C45,
  input  C46,
  input  C47,
  input  C48,
  input  C49,
  input  C50,
  input  C51,
  input  C52,
  input  C53,
  input  C54,
  input  C55,
  input  C56,
  input  C57,
  input  C58,
  input  C59,
  input  C60,
  input  C61,
  input  C62,
  input  C63,
  input  S1,
  input  S2,
  input  S3,
  input  S4,
  input  S5,
  input  S0,
  output out_71
);

  wire mux32_1_1_out_38, mux32_1_2_out_38;

  Mux32_1 mux32_1_1 (
    .C0(C32), .C1(C33), .C2(C34), .C3(C35), .C4(C36), .C5(C37), .C6(C38), .C7(C39), .C8(C40), .C9(C41),
    .C10(C42), .C11(C43), .C12(C44), .C13(C45), .C14(C46), .C15(C47), .C16(C48), .C17(C49), .C18(C50),
    .C19(C51), .C20(C52), .C21(C53), .C22(C54), .C23(C55), .C24(C56), .C25(C57), .C26(C58), .C27(C59),
    .C28(C60), .C29(C61), .C30(C62), .C31(C63), .S0(S1), .S1(S2), .S2(S3), .S3(S4), .S4(S5),
    .out_38(mux32_1_1_out_38));
  Mux32_1 mux32_1_2 (
    .C0(C0), .C1(C1), .C2(C2), .C3(C3), .C4(C4), .C5(C5), .C6(C6), .C7(C7), .C8(C8), .C9(C9), .C10(C10),
    .C11(C11), .C12(C12), .C13(C13), .C14(C14), .C15(C15), .C16(C16), .C17(C17), .C18(C18), .C19(C19),
    .C20(C20), .C21(C21), .C22(C22), .C23(C23), .C24(C24), .C25(C25), .C26(C26), .C27(C27), .C28(C28),
    .C29(C29), .C30(C30), .C31(C31), .S0(S1), .S1(S2), .S2(S3), .S3(S4), .S4(S5), .out_38(mux32_1_2_out_38));
  Mux2_1 mux2_1_1 (.A(mux32_1_2_out_38), .B(mux32_1_1_out_38), .Sel(S0), .out_4(out_71));
endmodule
