// Logisim project Operações.circ as structural Verilog: 4 circuits, main circuit Xnor_2
module Xnor_2 (
  input  in_1,
  input  in_2,
  output out_3
);

  xnor xnor_1 (out_3, in_1, in_2);

  // Notes on the sheet:
  //   0 + 0 = 1
  //   0 + 1 = 0
  //   1 + 0 = 0
  //   1 + 1 = 1
endmodule

module Xor_2 (
  input  in_1,
  input  in_2,
  output out_3
);

  xor xor_1 (out_3, in_1, in_2);

  // Notes on the sheet:
  //   0 + 0 = 0
  //   0 + 1 = 1
  //   1 + 0 = 1
  //   1 + 1 = 0
endmodule

module Nor_2 (
  input  in_1,
  input  in_2,
  output out_3
);

  nor nor_1 (out_3, in_1, in_2);

  // Notes on the sheet:
  //   0 + 0 = 1
  //   0 + 1 = 0
  //   1 + 0 = 0
  //   1 + 1 = 0
endmodule

module Nand_2 (
  input  in_1,
  input  in_2,
  output out_3
);

  nand nand_1 (out_3, in_1, in_2);

  // Notes on the sheet:
  //   0 + 0 = 1
  //   0 + 1 = 1
  //   1 + 0 = 1
  //   1 + 1 = 0
endmodule
