// Logisim project Somador.circ as structural Verilog: 1 circuit, main circuit main
module main (
  input  OP,
  input  V1,
  input  A,
  input  B,
  output SOMA
);

  wire and_1_out, and_2_out, and_3_out, and_4_out;

  and and_1 (and_1_out, ~B, A, ~V1);  // AND_Gate
  and and_2 (and_2_out, ~B, ~A, V1);  // AND_Gate
  and and_3 (and_3_out, B, ~A, ~V1);  // AND_Gate
  and and_4 (and_4_out, B, A, V1);
  or or_1 (SOMA, and_1_out, and_2_out, and_3_out, and_4_out);
endmodule
