// Logisim project Somador_Completo.circ as structural Verilog: 1 circuit, main circuit main
module main (
  input  C,
  input  A,
  input  B,
  input  \A¹ ,
  input  \B¹ ,
  input  \A² ,
  input  \B² ,
  input  \A³ ,
  input  \B³ ,
  output out_10,
  output out_11,
  output out_12,
  output out_13,
  output out_14
);

  wire and_1_out, and_2_out, and_3_out, and_4_out, and_5_out, and_6_out, and_7_out, and_8_out, and_9_out,
       and_10_out, and_11_out, and_12_out, and_13_out, and_14_out, or_1_out, or_2_out, xor_1_out, xor_2_out,
       xor_3_out, xor_4_out, xor_9_out;

  xor xor_1 (xor_1_out, B, A);
  and and_1 (and_1_out, A, B);
  xor xor_2 (xor_2_out, \B¹ , \A¹ );
  and and_2 (and_2_out, \A¹ , \B¹ );
  xor xor_3 (xor_3_out, \B² , \A² );
  and and_3 (and_3_out, \A² , \B² );
  xor xor_4 (xor_4_out, \B³ , \A³ );
  and and_4 (and_4_out, \A³ , \B³ );
  xor xor_5 (out_10, C, xor_1_out);
  xor xor_6 (out_11, or_1_out, xor_2_out);
  xor xor_7 (out_12, or_2_out, xor_3_out);
  xor xor_8 (out_13, xor_9_out, xor_4_out);
  or or_1 (or_1_out, and_1_out, and_5_out);
  or or_2 (or_2_out, and_2_out, and_6_out, and_7_out);
  ExactlyOne xor_9 (.out(xor_9_out), .in0(and_3_out), .in1(and_8_out), .in2(and_9_out), .in3(and_10_out));
  or or_3 (out_14, and_4_out, and_11_out, and_12_out, and_13_out, and_14_out);
  and and_5 (and_5_out, xor_1_out, C);
  and and_6 (and_6_out, xor_2_out, and_1_out);
  and and_7 (and_7_out, xor_2_out, and_1_out, C);
  and and_8 (and_8_out, xor_3_out, and_2_out);
  and and_9 (and_9_out, and_2_out, and_1_out, xor_1_out);
  and and_10 (and_10_out, xor_3_out, xor_2_out, and_1_out, C);
  and and_11 (and_11_out, xor_4_out, and_3_out);
  and and_12 (and_12_out, xor_4_out, xor_3_out, and_2_out);
  and and_13 (and_13_out, xor_4_out, xor_3_out, xor_2_out, and_1_out);
  and and_14 (and_14_out, xor_4_out, xor_3_out, xor_2_out, xor_1_out, C);
endmodule
