// Logisim project Somador_Nand.circ as structural Verilog: 1 circuit, main circuit main
module main (
  input  A,
  input  B,
  input  C,
  input  D,
  input  S0,
  input  S1,
  output out_7
);

  wire nand_1_out, nand_2_out, nand_3_out, nand_4_out, nand_5_out, nand_6_out, nand_7_out, nand_8_out,
       nand_9_out, nand_10_out, nand_11_out, nand_12_out, nand_13_out, nand_14_out;

  nand nand_1 (nand_1_out, S0, S0);
  nand nand_2 (nand_2_out, S1, S1);
  nand nand_3 (nand_3_out, nand_1_out, nand_2_out);
  nand nand_4 (nand_4_out, nand_1_out, S1);
  nand nand_5 (nand_5_out, S0, nand_2_out);
  nand nand_6 (nand_6_out, S0, S1);
  nand nand_7 (nand_7_out, nand_3_out, nand_3_out);
  nand nand_8 (nand_8_out, nand_4_out, nand_4_out);
  nand nand_9 (nand_9_out, nand_5_out, nand_5_out);
  nand nand_10 (nand_10_out, nand_6_out, nand_6_out);
  nand nand_11 (nand_11_out, A, nand_7_out);
  nand nand_12 (nand_12_out, B, nand_8_out);
  nand nand_13 (nand_13_out, C, nand_9_out);
  nand nand_14 (nand_14_out, D, nand_10_out);
  nand nand_15 (out_7, nand_11_out, nand_12_out, nand_13_out, nand_14_out);
endmodule
