// Logisim project ULA.circ as structural Verilog
module mux_4_1 (
  input  A,
  input  B,
  input  C,
  input  D,
  input  SEL_0,
  input  SEL_1,
  output out_7
);

  wire mux2_1_1_out_4, mux2_1_2_out_4;

  Mux2_1 mux2_1_1 (.in_1(A), .in_2(B), .in_3(SEL_1), .out_4(mux2_1_1_out_4));
  Mux2_1 mux2_1_2 (.in_1(C), .in_2(D), .in_3(SEL_1), .out_4(mux2_1_2_out_4));
  Mux2_1 mux2_1_3 (.in_1(mux2_1_1_out_4), .in_2(mux2_1_2_out_4), .in_3(SEL_0), .out_4(out_7));
endmodule

module Ula_braulio (
  input  [3:0] in_1,
  input  [3:0] in_2,
  output [3:0] out_3
);

  CelulaUla celulaula_1 ();
  CelulaUla celulaula_2 ();
  CelulaUla celulaula_3 ();
  CelulaUla celulaula_4 ();
  // Pins of 2 and 4 bits meet at out_3
  // Pins of 2 and 4 bits meet at in_1
  // Pins of 2 and 4 bits meet at in_2

  // Notes on the sheet:
  //   00 = and
  //   01 = or
  //   10 =soma
  //   11 = xor
endmodule

module ShiftleftArithmetic (
  input  [3:0] in_1,
  output [3:0] out_2
);


  assign out_2 = {in_1[2:0], 1'b0};
endmodule

module ShiftRightArithmetic (
  input  [3:0] in_1,
  output [3:0] out_2
);


  assign out_2 = {{2{in_1[3]}}, in_1[2:1]};
endmodule

module SLLdetect (
  input  [2:0] ULAOPCOde,
  output out_2
);

  and and_1 (out_2, ~ULAOPCOde[0], ~ULAOPCOde[1], ULAOPCOde[2]);  // AND_Gate
endmodule

module Mux2_1 (
  input  in_1,
  input  in_2,
  input  in_3,
  output out_4
);

  wire and_1_out, and_2_out;

  and and_1 (and_1_out, in_1, ~in_3);  // AND_Gate
  and and_2 (and_2_out, in_2, in_3);
  or or_1 (out_4, and_1_out, and_2_out);
endmodule

module FULL_ADDER (
  input  B,
  input  A,
  input  CARRY_IN,
  output CARRY_OUT,
  output out_5
);

  wire and_1_out, and_2_out, and_3_out, xor_1_out;

  or or_1 (CARRY_OUT, and_1_out, and_2_out, and_3_out);
  and and_1 (and_1_out, CARRY_IN, B);
  and and_2 (and_2_out, B, A);
  and and_3 (and_3_out, CARRY_IN, A);
  xor xor_1 (xor_1_out, B, A);
  xor xor_2 (out_5, CARRY_IN, xor_1_out);
endmodule

module ULALAU (
  input  SUB,
  input  CIN,
  input  A,
  input  B,
  input  [2:0] in_5,
  input  LESS,
  output out_7,
  output COUT,
  output SET
);

  wire and_1_out, nor_1_out, or_1_out, xnor_1_out, xor_1_out, xor_2_out;

  xor xor_1 (xor_1_out, A, A);
  and and_1 (and_1_out, A, A);
  or or_1 (or_1_out, A, A);
  xor xor_2 (xor_2_out, A, A);
  nor nor_1 (nor_1_out, A, A);
  FULL_ADDER full_adder_1 (.CARRY_OUT(COUT), .B(xor_1_out), .A(A), .out_5(SET), .CARRY_IN(CIN));
  xnor xnor_1 (xnor_1_out, A, A);
  Multiplexer #(.select(3)) multiplexer_1 (
    .in0(and_1_out), .in1(or_1_out), .in2(xor_2_out), .in3(nor_1_out), .in4(SET), .in5(LESS),
    .in6(xnor_1_out), .out(out_7), .sel(in_5));  // open: in7, en

  assign B = A;
  assign SUB = A;

  // Notes on the sheet:
  //   ALU OPERATORS
  //   AND
  //   OR
  //   XOR
  //   NOR
  //   ADD/SUB
  //   XNOR
endmodule

module ALU_8b (
  input  [7:0] in_1,
  input  in_2,
  input  [2:0] OP,
  input  [7:0] in_4,
  input  [7:0] R,
  output ZERO
);

  wire ulalau_1_cout, ulalau_2_cout, ulalau_3_cout, ulalau_4_cout, ulalau_5_cout, ulalau_6_cout,
       ulalau_7_cout, ulalau_8_set;

  ULALAU ulalau_1 (
    .A(in_1[0]), .B(in_4[0]), .LESS(ulalau_8_set), .out_7(R[0]), .SUB(in_2), .CIN(in_2),
    .COUT(ulalau_1_cout), .in_5(OP));  // open: SET
  ULALAU ulalau_2 (
    .A(in_1[1]), .B(in_4[1]), .LESS(1'b0), .out_7(R[1]), .SUB(in_2), .CIN(ulalau_1_cout),
    .COUT(ulalau_2_cout), .in_5(OP));  // open: SET
  ULALAU ulalau_3 (
    .A(in_1[2]), .B(in_4[2]), .LESS(1'b0), .out_7(R[2]), .SUB(in_2), .CIN(ulalau_2_cout),
    .COUT(ulalau_3_cout), .in_5(OP));  // open: SET
  ULALAU ulalau_4 (
    .A(in_1[3]), .B(in_4[3]), .LESS(1'b0), .out_7(R[3]), .SUB(in_2), .CIN(ulalau_3_cout),
    .COUT(ulalau_4_cout), .in_5(OP));  // open: SET
  ULALAU ulalau_5 (
    .A(in_1[4]), .B(in_4[4]), .LESS(1'b0), .out_7(R[4]), .SUB(in_2), .CIN(ulalau_4_cout),
    .COUT(ulalau_5_cout), .in_5(OP));  // open: SET
  ULALAU ulalau_6 (
    .A(in_1[5]), .B(in_4[5]), .LESS(1'b0), .out_7(R[5]), .SUB(in_2), .CIN(ulalau_5_cout),
    .COUT(ulalau_6_cout), .in_5(OP));  // open: SET
  ULALAU ulalau_7 (
    .A(in_1[6]), .B(in_4[6]), .LESS(1'b0), .out_7(R[6]), .SUB(in_2), .CIN(ulalau_6_cout),
    .COUT(ulalau_7_cout), .in_5(OP));  // open: SET
  ULALAU ulalau_8 (
    .A(in_1[7]), .B(in_4[7]), .LESS(1'b0), .out_7(R[7]), .SUB(in_2), .CIN(ulalau_7_cout), .SET(ulalau_8_set),
    .in_5(OP));  // open: COUT
  nor nor_1 (ZERO, R[0], R[1], R[2], R[3], R[4], R[5], R[6], R[7]);
endmodule

module Alu_2b (
  input  [1:0] A,
  input  in_2,
  input  [2:0] in_3,
  input  [1:0] B,
  output [1:0] out_5,
  output out_6
);

  wire ulalau_1_cout, ulalau_2_set;

  ULALAU ulalau_1 (
    .A(A[0]), .B(B[0]), .LESS(ulalau_2_set), .out_7(out_5[0]), .SUB(in_2), .CIN(in_2), .COUT(ulalau_1_cout),
    .in_5(in_3));  // open: SET
  ULALAU ulalau_2 (
    .A(A[1]), .B(B[1]), .LESS(1'b0), .out_7(out_5[1]), .SUB(in_2), .CIN(ulalau_1_cout), .SET(ulalau_2_set),
    .in_5(in_3));  // open: COUT
  nor nor_1 (out_6, out_5[0], out_5[1]);
endmodule

module mux_8_1 (
  input  A,
  input  B,
  input  C,
  input  D,
  input  E,
  input  F,
  input  G,
  input  H,
  input  SEL_0,
  input  SEL_1,
  input  SEL_2,
  output out_12
);

  wire mux_4_1_1_out_7, mux_4_1_2_out_7;

  mux_4_1 mux_4_1_1 (.A(A), .B(B), .C(C), .D(D), .SEL_0(SEL_1), .SEL_1(SEL_2), .out_7(mux_4_1_1_out_7));
  mux_4_1 mux_4_1_2 (.A(E), .B(F), .C(G), .D(H), .SEL_0(SEL_1), .SEL_1(SEL_2), .out_7(mux_4_1_2_out_7));
  Mux2_1 mux2_1_1 (.in_1(mux_4_1_1_out_7), .in_2(mux_4_1_2_out_7), .in_3(SEL_0), .out_4(out_12));
endmodule

module mux_16_1 (
  input  A,
  input  B,
  input  C,
  input  D,
  input  E,
  input  F,
  input  G,
  input  H,
  input  I,
  input  J,
  input  K,
  input  L,
  input  M,
  input  N,
  input  O,
  input  P,
  input  S0,
  input  S1,
  input  S2,
  input  S3,
  output out_21
);

  wire mux_8_1_1_out_12, mux_8_1_2_out_12;

  mux_8_1 mux_8_1_1 (
    .A(I), .B(J), .C(K), .D(L), .E(M), .F(N), .G(O), .H(P), .SEL_0(S1), .SEL_1(S2), .SEL_2(S3),
    .out_12(mux_8_1_1_out_12));
  mux_8_1 mux_8_1_2 (
    .A(A), .B(B), .C(C), .D(D), .E(E), .F(F), .G(G), .H(H), .SEL_0(S1), .SEL_1(S2), .SEL_2(S3),
    .out_12(mux_8_1_2_out_12));
  Mux2_1 mux2_1_1 (.in_1(mux_8_1_2_out_12), .in_2(mux_8_1_1_out_12), .in_3(S0), .out_4(out_21));
endmodule

module mux_32_1 (
  input  C0,
  input  C1,
  input  C2,
  input  C3,
  input  C4,
  input  C5,
  input  C6,
  input  C7,
  input  C8,
  input  C9,
  input  C10,
  input  C11,
  input  C12,
  input  C13,
  input  C14,
  input  C15,
  input  C16,
  input  C17,
  input  C18,
  input  C19,
  input  C20,
  input  C21,
  input  C22,
  input  C23,
  input  C24,
  input  C25,
  input  C26,
  input  C27,
  input  C28,
  input  C29,
  input  C30,
  input  C31,
  input  S0,
  input  S1,
  input  S2,
  input  S3,
  input  S4,
  output out_38
);

  wire mux_16_1_1_out_21, mux_16_1_2_out_21;

  mux_16_1 mux_16_1_1 (
    .A(C16), .B(C17), .C(C18), .D(C19), .E(C20), .F(C21), .G(C22), .H(C23), .I(C24), .J(C25), .K(C26),
    .L(C27), .M(C28), .N(C29), .O(C30), .P(C31), .S0(S1), .S1(S2), .S2(S3), .S3(S4),
    .out_21(mux_16_1_1_out_21));
  mux_16_1 mux_16_1_2 (
    .A(C0), .B(C1), .C(C2), .D(C3), .E(C4), .F(C5), .G(C6), .H(C7), .I(C8), .J(C9), .K(C10), .L(C11),
    .M(C12), .N(C13), .O(C14), .P(C15), .S0(S1), .S1(S2), .S2(S3), .S3(S4), .out_21(mux_16_1_2_out_21));
  Mux2_1 mux2_1_1 (.in_1(mux_16_1_2_out_21), .in_2(mux_16_1_1_out_21), .in_3(S0), .out_4(out_38));
endmodule
