// Logisim project test.circ as structural Verilog: 7 circuits, main circuit main
module main (
  input  A,
  input  B,
  input  Sel,
  output out_4
);

  wire and_1_out, and_2_out;

  and and_1 (and_1_out, A, ~Sel);  // AND_Gate
  and and_2 (and_2_out, B, Sel);
  or or_1 (out_4, and_1_out, and_2_out);
endmodule

module Celula_Ula (
  input  in_1,
  input  in_2,
  input  in_3,
  input  in_4,
  output out_5,
  output out_6
);

  wire and_1_out, or_1_out, undriven, xor_1_out;

  and and_1 (and_1_out, in_1, in_2);
  or or_1 (or_1_out, in_1, in_2);
  xor xor_1 (xor_1_out, in_1, in_2);
  mux_4 mux_4_1 (.A(and_1_out), .B(or_1_out), .C(xor_1_out), .D(undriven), .SEL_0(in_4), .out_7(out_5));  // open: SEL_1
endmodule

module mux_4 (
  input  A,
  input  B,
  input  C,
  input  D,
  input  SEL_0,
  input  SEL_1,
  output out_7
);

  wire main_1_out_4, main_2_out_4;

  main main_1 (.A(C), .B(D), .Sel(SEL_1), .out_4(main_1_out_4));
  main main_2 (.A(A), .B(B), .Sel(SEL_1), .out_4(main_2_out_4));
  main main_3 (.A(main_2_out_4), .B(main_1_out_4), .Sel(SEL_0), .out_4(out_7));
endmodule

module Ula_4b (
  input  [3:0] in_1,
  input  [3:0] in_2,
  output [3:0] out_3
);

  wire celula_ula_4_out_5;

  Celula_Ula celula_ula_1 ();  // open: in_1, in_2, out_6, in_4, out_5, in_3
  Celula_Ula celula_ula_2 ();  // open: in_1, in_2, out_6, in_4, out_5, in_3
  Celula_Ula celula_ula_3 ();  // open: in_1, in_2, out_6, in_4, out_5, in_3
  Celula_Ula celula_ula_4 (.out_5(celula_ula_4_out_5));  // open: in_1, in_2, out_6, in_4, in_3
  // Pins of 2 and 4 bits meet at out_3
  // Pins of 2 and 4 bits meet at in_1
  // Pins of 2 and 4 bits meet at in_2
  // also tied to GND on the sheet: celula_ula_4_out_5

  // Notes on the sheet:
  //   00 = and
  //   01 = or
  //   10 =soma
  //   11 = xor
endmodule

module Shift_Left_Logic (
  input  [3:0] in_1,
  output [3:0] out_2
);


  assign out_2 = {in_1[2:0], 1'b0};
endmodule

module Shift_Right_Arithmetic (
  input  [3:0] in_1,
  output [3:0] out_2
);


  assign out_2 = {{2{in_1[3]}}, in_1[2:1]};
endmodule

module SLLdetect (
  input  [2:0] ULAOPCOde,
  output out_2
);

  and and_1 (out_2, ~ULAOPCOde[0], ~ULAOPCOde[1], ULAOPCOde[2]);  // AND_Gate
endmodule
