// Logisim project tentativa.circ as structural Verilog
module mux2 (
  input  A,
  input  B,
  input  Sel,
  output S
);

  wire and_1_out, and_2_out;

  and and_1 (and_1_out, A, ~Sel);  // AND_Gate
  and and_2 (and_2_out, B, Sel);
  LED led_1 (.in(and_1_out));
  or or_1 (S, and_1_out, and_2_out);
  LED led_2 (.in(and_2_out));
endmodule

module mux2b (
  input  [31:0] A,
  input  [31:0] B,
  input  Sel,
  output [31:0] S
);

  wire [31:0] and_1_out, and_2_out;

  assign and_1_out = A & ~{32{Sel}};  // AND_Gate and_1, 32 bits wide
  assign and_2_out = B & {32{Sel}};  // AND_Gate and_2, 32 bits wide
  assign S = and_1_out | and_2_out;  // OR_Gate or_1, 32 bits wide
endmodule

module mux4 (
  input  A,
  input  B,
  input  C,
  input  D,
  input  Sel1,
  input  Sel0,
  output out_7
);

  wire mux2_1_s, mux2_2_s;

  mux2 mux2_1 (.A(A), .B(B), .Sel(Sel0), .S(mux2_1_s));
  mux2 mux2_2 (.A(C), .B(D), .Sel(Sel0), .S(mux2_2_s));
  mux2 mux2_3 (.A(mux2_1_s), .B(mux2_2_s), .Sel(Sel1), .S(out_7));
endmodule

module mux4b (
  input  A,
  input  B,
  input  C,
  input  D,
  input  [1:0] in_5,
  output out_6
);

  wire mux2_1_s, mux2_2_s;

  mux2 mux2_1 (.A(A), .B(B), .Sel(in_5[0]), .S(mux2_1_s));
  mux2 mux2_2 (.A(C), .B(D), .Sel(in_5[0]), .S(mux2_2_s));
  mux2 mux2_3 (.A(mux2_1_s), .B(mux2_2_s), .Sel(in_5[1]), .S(out_6));
endmodule

module mux8 (
  input  l0,
  input  l1,
  input  l2,
  input  l3,
  input  l4,
  input  l5,
  input  l6,
  input  l7,
  input  in_9,
  input  in_10,
  input  in_11,
  output out_12
);

  wire mux4_1_out_7, mux4_2_out_7;

  mux4 mux4_1 (.A(l0), .B(l1), .C(l2), .D(l3), .Sel1(in_10), .Sel0(in_11), .out_7(mux4_1_out_7));
  mux4 mux4_2 (.A(l4), .B(l5), .C(l6), .D(l7), .Sel1(in_10), .Sel0(in_11), .out_7(mux4_2_out_7));
  mux2 mux2_1 (.A(mux4_1_out_7), .B(mux4_2_out_7), .Sel(in_9), .S(out_12));
endmodule

module mux8b (
  input  l0,
  input  l1,
  input  l2,
  input  l3,
  input  l4,
  input  l5,
  input  l6,
  input  l7,
  input  [2:0] in_9,
  output out_10
);

  wire mux4_1_out_7, mux4_2_out_7;

  mux4 mux4_1 (.A(l0), .B(l1), .C(l2), .D(l3), .Sel1(in_9[1]), .Sel0(in_9[0]), .out_7(mux4_1_out_7));
  mux4 mux4_2 (.A(l4), .B(l5), .C(l6), .D(l7), .Sel1(in_9[1]), .Sel0(in_9[0]), .out_7(mux4_2_out_7));
  mux2 mux2_1 (.A(mux4_1_out_7), .B(mux4_2_out_7), .Sel(in_9[2]), .S(out_10));
endmodule

module mux16 (
  input  l0,
  input  l1,
  input  l2,
  input  l3,
  input  l4,
  input  l5,
  input  l6,
  input  l7,
  input  l8,
  input  l9,
  input  l10,
  input  l11,
  input  l12,
  input  l13,
  input  l14,
  input  l15,
  input  in_17,
  input  in_18,
  input  in_19,
  input  in_20,
  output out_21
);

  wire mux8_1_out_12, mux8_2_out_12;

  mux8 mux8_1 (
    .l0(l0), .l1(l1), .l2(l2), .l3(l3), .l4(l4), .l5(l5), .l6(l6), .l7(l7), .in_9(in_18), .in_10(in_19),
    .in_11(in_20), .out_12(mux8_1_out_12));
  mux8 mux8_2 (
    .l0(l8), .l1(l9), .l2(l10), .l3(l11), .l4(l12), .l5(l13), .l6(l14), .l7(l15), .in_9(in_18),
    .in_10(in_19), .in_11(in_20), .out_12(mux8_2_out_12));
  mux2 mux2_1 (.A(mux8_1_out_12), .B(mux8_2_out_12), .Sel(in_17), .S(out_21));
endmodule

module mux16b (
  input  l0,
  input  l1,
  input  l2,
  input  l3,
  input  l4,
  input  l5,
  input  l6,
  input  l7,
  input  l8,
  input  l9,
  input  l10,
  input  l11,
  input  l12,
  input  l13,
  input  l14,
  input  l15,
  input  [3:0] in_17,
  output out_18
);

  wire mux8_1_out_12, mux8_2_out_12;

  mux8 mux8_1 (
    .l0(l0), .l1(l1), .l2(l2), .l3(l3), .l4(l4), .l5(l5), .l6(l6), .l7(l7), .in_9(in_17[2]),
    .in_10(in_17[1]), .in_11(in_17[0]), .out_12(mux8_1_out_12));
  mux8 mux8_2 (
    .l0(l8), .l1(l9), .l2(l10), .l3(l11), .l4(l12), .l5(l13), .l6(l14), .l7(l15), .in_9(in_17[2]),
    .in_10(in_17[1]), .in_11(in_17[0]), .out_12(mux8_2_out_12));
  mux2 mux2_1 (.A(mux8_1_out_12), .B(mux8_2_out_12), .Sel(in_17[3]), .S(out_18));
endmodule

module mux32 (
  input  l0,
  input  l1,
  input  l2,
  input  l3,
  input  l4,
  input  l5,
  input  l6,
  input  l7,
  input  l8,
  input  l9,
  input  l10,
  input  l11,
  input  l12,
  input  l13,
  input  l14,
  input  l15,
  input  l16,
  input  l17,
  input  l18,
  input  l19,
  input  l20,
  input  l21,
  input  l22,
  input  l23,
  input  l24,
  input  l25,
  input  l26,
  input  l27,
  input  l28,
  input  l29,
  input  l30,
  input  sel5,
  input  sel3,
  input  sel2,
  input  sel1,
  input  sel0,
  input  l31,
  output out_38
);

  wire mux16_1_out_21, mux16_2_out_21;

  mux16 mux16_1 (
    .l0(l0), .l1(l1), .l2(l2), .l3(l3), .l4(l4), .l5(l5), .l6(l6), .l7(l7), .l8(l8), .l9(l9), .l10(l10),
    .l11(l11), .l12(l12), .l13(l13), .l14(l14), .l15(l15), .in_17(sel3), .in_18(sel2), .in_19(sel1),
    .in_20(sel0), .out_21(mux16_1_out_21));
  mux16 mux16_2 (
    .l0(l16), .l1(l17), .l2(l18), .l3(l19), .l4(l20), .l5(l21), .l6(l22), .l7(l23), .l8(l24), .l9(l25),
    .l10(l26), .l11(l27), .l12(l28), .l13(l29), .l14(l30), .l15(l31), .in_17(sel3), .in_18(sel2),
    .in_19(sel1), .in_20(sel0), .out_21(mux16_2_out_21));
  mux2 mux2_1 (.A(mux16_1_out_21), .B(mux16_2_out_21), .Sel(sel5), .S(out_38));
endmodule

module mux32b (
  input  l0,
  input  l1,
  input  l2,
  input  l3,
  input  l4,
  input  l5,
  input  l6,
  input  l7,
  input  l8,
  input  l9,
  input  l10,
  input  l11,
  input  l12,
  input  l13,
  input  l14,
  input  l15,
  input  l16,
  input  l17,
  input  l18,
  input  l19,
  input  l20,
  input  l21,
  input  l22,
  input  l23,
  input  l24,
  input  l25,
  input  l26,
  input  l27,
  input  l28,
  input  l29,
  input  l30,
  input  l31,
  input  [4:0] in_33,
  output out_34
);

  wire mux16_1_out_21, mux16_2_out_21;

  mux16 mux16_1 (
    .l0(l0), .l1(l1), .l2(l2), .l3(l3), .l4(l4), .l5(l5), .l6(l6), .l7(l7), .l8(l8), .l9(l9), .l10(l10),
    .l11(l11), .l12(l12), .l13(l13), .l14(l14), .l15(l15), .in_17(in_33[3]), .in_18(in_33[2]),
    .in_19(in_33[1]), .in_20(in_33[0]), .out_21(mux16_1_out_21));
  mux16 mux16_2 (
    .l0(l16), .l1(l17), .l2(l18), .l3(l19), .l4(l20), .l5(l21), .l6(l22), .l7(l23), .l8(l24), .l9(l25),
    .l10(l26), .l11(l27), .l12(l28), .l13(l29), .l14(l30), .l15(l31), .in_17(in_33[3]), .in_18(in_33[2]),
    .in_19(in_33[1]), .in_20(in_33[0]), .out_21(mux16_2_out_21));
  mux2 mux2_1 (.A(mux16_1_out_21), .B(mux16_2_out_21), .Sel(in_33[4]), .S(out_34));
endmodule

module SubFULL (
  input  A,
  input  B,
  input  Bin,
  output d,
  output b_2
);

  wire and_1_out, and_2_out, xor_1_out;

  xor xor_1 (xor_1_out, A, B);
  xor xor_2 (d, xor_1_out, Bin);
  and and_1 (and_1_out, ~xor_1_out, Bin);  // AND_Gate
  and and_2 (and_2_out, ~A, B);  // AND_Gate
  or or_1 (b_2, and_1_out, and_2_out);
endmodule

module Fullsubtractor (
  input  V1,
  input  B,
  input  A,
  output out_4,
  output out_5
);

  wire and_1_out, and_2_out, and_3_out, and_4_out, and_5_out, and_6_out, and_7_out;

  and and_1 (and_1_out, ~A, ~B, V1);  // AND_Gate
  and and_2 (and_2_out, ~A, B, ~V1);  // AND_Gate
  and and_3 (and_3_out, A, ~B, ~V1);  // AND_Gate
  and and_4 (and_4_out, A, B, V1);
  and and_5 (and_5_out, ~A, V1);  // AND_Gate
  and and_6 (and_6_out, ~A, B);  // AND_Gate
  and and_7 (and_7_out, B, V1);
  or or_1 (out_4, and_1_out, and_2_out, and_3_out, and_4_out);
  or or_2 (out_5, and_5_out, and_6_out, and_7_out);
endmodule

module FullSubtratctor32bit (
  input  [31:0] V1,
  input  [31:0] B,
  input  [31:0] A,
  output [31:0] out_4,
  output [31:0] out_5
);

  wire [31:0] and_1_out, and_2_out, and_3_out, and_4_out, and_5_out, and_6_out, and_7_out;

  assign and_1_out = ~A & ~B & V1;  // AND_Gate and_1, 32 bits wide
  assign and_2_out = ~A & B & ~V1;  // AND_Gate and_2, 32 bits wide
  assign and_3_out = A & ~B & ~V1;  // AND_Gate and_3, 32 bits wide
  assign and_4_out = A & B & V1;  // AND_Gate and_4, 32 bits wide
  assign and_5_out = ~A & V1;  // AND_Gate and_5, 32 bits wide
  assign and_6_out = ~A & B;  // AND_Gate and_6, 32 bits wide
  assign and_7_out = B & V1;  // AND_Gate and_7, 32 bits wide
  assign out_4 = and_1_out | and_2_out | and_3_out | and_4_out;  // OR_Gate or_1, 32 bits wide
  assign out_5 = and_5_out | and_6_out | and_7_out;  // OR_Gate or_2, 32 bits wide
endmodule

module FullAdder (
  input  vem1,
  input  B,
  input  A,
  output soma,
  output vai1
);

  wire and_1_out, and_2_out, and_3_out, and_4_out, or_1_out, xnor_1_out, xor_1_out;

  xnor xnor_1 (xnor_1_out, B, A);
  xor xor_1 (xor_1_out, B, A);
  or or_1 (or_1_out, B, A);
  and and_1 (and_1_out, B, A);
  and and_2 (and_2_out, or_1_out, vem1);
  and and_3 (and_3_out, xnor_1_out, vem1);
  and and_4 (and_4_out, xor_1_out, ~vem1);  // AND_Gate
  or or_2 (vai1, and_1_out, and_2_out);
  or or_3 (soma, and_3_out, and_4_out);
endmodule

module FullAdder4bits (
  input  [3:0] vem1,
  input  [3:0] B,
  input  [3:0] A,
  output [3:0] soma,
  output [3:0] vai1
);

  wire [3:0] and_1_out, and_2_out, and_3_out, and_4_out, or_1_out, xnor_1_out, xor_1_out;

  Hex_Digit_Display hex_digit_display_1 (.value(vem1));  // open: dp
  Hex_Digit_Display hex_digit_display_2 (.value(A));  // open: dp
  Hex_Digit_Display hex_digit_display_3 (.value(B));  // open: dp
  assign xnor_1_out = ~(B ^ A);  // XNOR_Gate xnor_1, 4 bits wide
  assign xor_1_out = B ^ A;  // XOR_Gate xor_1, 4 bits wide
  assign or_1_out = B | A;  // OR_Gate or_1, 4 bits wide
  assign and_1_out = B & A;  // AND_Gate and_1, 4 bits wide
  assign and_2_out = or_1_out & vem1;  // AND_Gate and_2, 4 bits wide
  assign and_3_out = xnor_1_out & vem1;  // AND_Gate and_3, 4 bits wide
  assign and_4_out = xor_1_out & ~vem1;  // AND_Gate and_4, 4 bits wide
  assign vai1 = and_1_out | and_2_out;  // OR_Gate or_2, 4 bits wide
  Hex_Digit_Display hex_digit_display_4 (.value(soma));  // open: dp
  assign soma = and_3_out | and_4_out;  // OR_Gate or_3, 4 bits wide
  Hex_Digit_Display hex_digit_display_5 (.value(vai1));  // open: dp
endmodule

module ULACell_DeuErro (
  input  b,
  input  a,
  input  vem1,
  input  bin,
  input  [4:0] OpCode,
  output saida,
  output vai1,
  output b_2
);

  wire and_1_out, fulladder_1_soma, nand_1_out, nor_1_out, not_1_out, not_2_out, not_3_out, not_4_out,
       or_1_out, subfull_1_d, xnor_1_out, xor_1_out;

  and and_1 (and_1_out, b, a);
  or or_1 (or_1_out, b, a);
  FullAdder fulladder_1 (.B(b), .A(a), .vem1(vem1), .vai1(vai1), .soma(fulladder_1_soma));
  xor xor_1 (xor_1_out, b, a);
  SubFULL subfull_1 (.A(a), .B(b), .Bin(bin), .d(subfull_1_d), .b_2(b_2));
  not not_1 (not_1_out, fulladder_1_soma);
  not not_2 (not_2_out, b_2);
  nand nand_1 (nand_1_out, b, a);
  nor nor_1 (nor_1_out, b, a);
  xnor xnor_1 (xnor_1_out, b, a);
  not not_3 (not_3_out, a);
  not not_4 (not_4_out, b);
  mux32b mux32b_1 (
    .l0(and_1_out), .l1(or_1_out), .l2(fulladder_1_soma), .l3(xor_1_out), .l4(a), .l5(b), .l6(a), .l7(b),
    .l8(a), .l9(b), .l10(a), .l11(b), .l12(subfull_1_d), .l13(nand_1_out), .l14(nor_1_out), .l15(xnor_1_out),
    .l16(not_3_out), .l17(not_4_out), .l18(not_1_out), .l19(not_2_out), .l20(a), .l21(b), .in_33(OpCode),
    .out_34(saida));  // open: l22, l23, l24, l25, l26, l27, l28, l29, l30, l31

  // Notes on the sheet:
  //   00000 - AND
  //   00001 - OR
  //   00011 - XOR
  //   01110 - NOR
  //   10100 - A
  //   10101 - B
  //   00010 - SOMADOR
  //   00100 - SLL A
  //   00101 - SLL B
  //   00110 - SRL A
  //   00111 - SRL B
  //   01000 - SLA A
  //   01001 - SLA B
  //   01010 - SRA A
  //   01011 - SRA B
  //   01100 - SUBTRACTOR
  //   01101 - NAND
  //   01111 - XNOR
  //   10000 - NOT A
  //   10001 - NOT B
  //   10010 - NOT A+B
  //   10011 - NOT A-B
endmodule

module Ulacell (
  input  a,
  input  b,
  input  vem1,
  input  [4:0] OpCode,
  output saida,
  output vai1
);

  wire and_1_out, fulladder_1_soma, nand_1_out, nand_2_out, nor_1_out, not_1_out, not_2_out, not_3_out,
       or_1_out, xnor_1_out, xor_1_out;

  and and_1 (and_1_out, a, a);
  or or_1 (or_1_out, a, a);
  FullAdder fulladder_1 (.B(a), .A(a), .vem1(vem1), .vai1(vai1), .soma(fulladder_1_soma));
  xor xor_1 (xor_1_out, a, a);
  not not_1 (not_1_out, fulladder_1_soma);
  nand nand_1 (nand_1_out, a, a);
  nor nor_1 (nor_1_out, a, a);
  xnor xnor_1 (xnor_1_out, a, a);
  not not_2 (not_2_out, a);
  not not_3 (not_3_out, a);
  nand nand_2 (nand_2_out, ~a, a);  // NAND_Gate
  mux32b mux32b_1 (
    .l0(and_1_out), .l1(or_1_out), .l2(fulladder_1_soma), .l3(xor_1_out), .l4(a), .l5(a), .l6(a), .l7(a),
    .l8(a), .l9(a), .l10(a), .l11(a), .l12(nand_1_out), .l13(nor_1_out), .l14(xnor_1_out), .l15(not_2_out),
    .l16(not_3_out), .l17(not_1_out), .l18(a), .l19(a), .l31(nand_2_out), .in_33(OpCode), .out_34(saida));  // open: l20, l21, l22, l23, l24, l25, l26, l27, l28, l29, l30

  assign b = a;

  // Notes on the sheet:
  //   00000 - AND
  //   00001 - OR
  //   00010 - SOMADOR
  //   00011 - XOR
  //   00100 - SLL A
  //   00101 - SLL B
  //   00110 - SRL A
  //   00111 - SRL B
  //   01000 - SLA A
  //   01001 - SLA B
  //   01010 - SRA A
  //   01011 - SRA B
  //   01100 - NAND
  //   01101 - NOR
  //   01110 - XNOR
  //   01111 - NOT B
  //   10000 - NOT A
  //   10001 - NOT A+B
  //   10010 - B
  //   10011 - A
  //   10100 - A AND NOT B
  //   10101 - NOT A AND B
  //   10110 - NOT A AND NOT B
endmodule

module ShiftLeftLogical32bit (
  input  [31:0] in_1,
  input  Shift,
  output [31:0] out_3
);

  mux2b mux2b_1 (.A(in_1), .B({in_1[30:0], 1'b0}), .Sel(Shift), .S(out_3));
endmodule

module ShiftLeftArith32bit (
  input  [31:0] in_1,
  input  Shift,
  output [31:0] out_3
);

  mux2b mux2b_1 (.A(in_1), .B({in_1[30:0], in_1[0]}), .Sel(Shift), .S(out_3));
endmodule

module ShiftRightLogical32bit (
  input  [31:0] in_1,
  input  Shift,
  output [31:0] out_3
);

  mux2b mux2b_1 (.A(in_1), .B({1'b0, in_1[31:1]}), .Sel(Shift), .S(out_3));
endmodule

module ShiftRightArith32bit (
  input  [31:0] in_1,
  input  Shift,
  output [31:0] out_3
);

  mux2b mux2b_1 (.A(in_1), .B({{2{in_1[31]}}, in_1[30:1]}), .Sel(Shift), .S(out_3));
endmodule

module SLLDetect (
  input  [4:0] ALUOpCode,
  output sll
);

  and and_1 (sll, ~ALUOpCode[0], ~ALUOpCode[1], ~ALUOpCode[2], ~ALUOpCode[3], ALUOpCode[4]);  // AND_Gate
endmodule

module SLLADetector (
  input  [4:0] UlaOpCode,
  output out_2
);

  and and_1 (out_2, ~UlaOpCode[0], ~UlaOpCode[1], UlaOpCode[2], ~UlaOpCode[3], ~UlaOpCode[4]);  // AND_Gate
endmodule

module SLLBDetector (
  input  [4:0] UlaOpCode,
  output saida
);

  and and_1 (saida, ~UlaOpCode[4], ~UlaOpCode[3], UlaOpCode[2], ~UlaOpCode[1], UlaOpCode[0]);  // AND_Gate
endmodule

module SRLADetector (
  input  [4:0] UlaOpCode,
  output out_2
);

  and and_1 (out_2, ~UlaOpCode[0], UlaOpCode[1], UlaOpCode[2], ~UlaOpCode[3], ~UlaOpCode[4]);  // AND_Gate
endmodule

module SRLBDetector (
  input  [4:0] UlaOpCode,
  output out_2
);

  and and_1 (out_2, ~UlaOpCode[4], ~UlaOpCode[3], UlaOpCode[2], UlaOpCode[1], UlaOpCode[0]);  // AND_Gate
endmodule

module SLAADetector (
  input  [4:0] UlaOpCode,
  output out_2
);

  and and_1 (out_2, ~UlaOpCode[4], UlaOpCode[3], ~UlaOpCode[2], ~UlaOpCode[1], ~UlaOpCode[0]);  // AND_Gate
endmodule

module SLABDetector (
  input  [4:0] UlaOpCode,
  output out_2
);

  and and_1 (out_2, ~UlaOpCode[4], UlaOpCode[3], ~UlaOpCode[2], ~UlaOpCode[1], UlaOpCode[0]);  // AND_Gate
endmodule

module SRAADetector (
  input  [4:0] UlaOpCode,
  output out_2
);

  and and_1 (out_2, ~UlaOpCode[4], UlaOpCode[3], ~UlaOpCode[2], UlaOpCode[1], ~UlaOpCode[0]);  // AND_Gate
endmodule

module SRABDetector (
  input  [4:0] UlaOpCode,
  output out_2
);

  and and_1 (out_2, ~UlaOpCode[4], UlaOpCode[3], ~UlaOpCode[2], UlaOpCode[1], UlaOpCode[0]);  // AND_Gate
endmodule

module ULA_DeuErro (
  input  [31:0] B,
  input  [31:0] A,
  input  [4:0] ULAOpCode,
  output out_4,
  output [31:0] R
);

  wire slaadetector_1_out_2, slabdetector_1_out_2, slladetector_1_out_2, sllbdetector_1_saida,
       sraadetector_1_out_2, srabdetector_1_out_2, srladetector_1_out_2, srlbdetector_1_out_2,
       ulacell_1_vai1, ulacell_3_vai1, ulacell_4_vai1, ulacell_5_vai1, ulacell_6_vai1, ulacell_7_vai1,
       ulacell_8_vai1, ulacell_9_vai1, ulacell_10_vai1, ulacell_11_vai1, ulacell_12_vai1, ulacell_13_vai1,
       ulacell_14_vai1, ulacell_15_vai1, ulacell_16_vai1, ulacell_17_vai1, ulacell_18_vai1, ulacell_19_vai1,
       ulacell_20_vai1, ulacell_21_vai1, ulacell_22_vai1, ulacell_23_vai1, ulacell_24_vai1, ulacell_25_vai1,
       ulacell_26_vai1, ulacell_27_vai1, ulacell_28_vai1, ulacell_29_vai1, ulacell_30_vai1, ulacell_31_vai1,
       ulacell_32_vai1;
  wire [30:0] shiftrightarith32bit_1_out_3;
  wire [31:0] shiftleftarith32bit_1_out_3, shiftleftarith32bit_2_out_3, shiftleftlogical32bit_1_out_3,
       shiftleftlogical32bit_2_out_3, shiftrightlogical32bit_1_out_3, shiftrightlogical32bit_2_out_3;
  wire [31:30] shiftrightarith32bit_2_out_3;

  ShiftLeftLogical32bit shiftleftlogical32bit_1 (
    .in_1(B), .Shift(sllbdetector_1_saida), .out_3(shiftleftlogical32bit_1_out_3));
  SLLBDetector sllbdetector_1 (.saida(sllbdetector_1_saida), .UlaOpCode(ULAOpCode));
  ShiftLeftLogical32bit shiftleftlogical32bit_2 (
    .in_1(A), .Shift(slladetector_1_out_2), .out_3(shiftleftlogical32bit_2_out_3));
  SRLADetector srladetector_1 (.out_2(srladetector_1_out_2), .UlaOpCode(ULAOpCode));
  SLLADetector slladetector_1 (.out_2(slladetector_1_out_2), .UlaOpCode(ULAOpCode));
  ShiftRightLogical32bit shiftrightlogical32bit_1 (
    .in_1(shiftleftlogical32bit_1_out_3), .Shift(srlbdetector_1_out_2), .out_3(shiftrightlogical32bit_1_out_3));
  ShiftLeftArith32bit shiftleftarith32bit_1 (
    .in_1(shiftrightlogical32bit_1_out_3), .Shift(slabdetector_1_out_2), .out_3(shiftleftarith32bit_1_out_3));
  SRLBDetector srlbdetector_1 (.out_2(srlbdetector_1_out_2), .UlaOpCode(ULAOpCode));
  SLABDetector slabdetector_1 (.out_2(slabdetector_1_out_2), .UlaOpCode(ULAOpCode));
  ShiftRightLogical32bit shiftrightlogical32bit_2 (
    .in_1(shiftleftlogical32bit_2_out_3), .Shift(srladetector_1_out_2), .out_3(shiftrightlogical32bit_2_out_3));
  SLAADetector slaadetector_1 (.out_2(slaadetector_1_out_2), .UlaOpCode(ULAOpCode));
  ShiftRightArith32bit shiftrightarith32bit_1 (
    .in_1(shiftleftarith32bit_1_out_3), .Shift(srabdetector_1_out_2),
    .out_3({shiftrightarith32bit_2_out_3[30], shiftrightarith32bit_1_out_3}));
  SRABDetector srabdetector_1 (.out_2(srabdetector_1_out_2), .UlaOpCode(ULAOpCode));
  ShiftRightArith32bit shiftrightarith32bit_2 (
    .in_1(shiftleftarith32bit_2_out_3), .Shift(sraadetector_1_out_2),
    .out_3({shiftrightarith32bit_2_out_3, {30{shiftrightarith32bit_2_out_3[30]}}}));
  ShiftLeftArith32bit shiftleftarith32bit_2 (
    .in_1(shiftrightlogical32bit_2_out_3), .Shift(slaadetector_1_out_2), .out_3(shiftleftarith32bit_2_out_3));
  SRAADetector sraadetector_1 (.out_2(sraadetector_1_out_2), .UlaOpCode(ULAOpCode));
  Ulacell ulacell_1 (
    .vai1(ulacell_1_vai1), .a(shiftrightarith32bit_2_out_3[30]), .b(shiftrightarith32bit_1_out_3[30]),
    .OpCode(ULAOpCode), .saida(R[30]), .vem1(ulacell_3_vai1));
  Ulacell ulacell_2 (
    .vai1(out_4), .a(shiftrightarith32bit_2_out_3[31]), .b(shiftrightarith32bit_2_out_3[30]),
    .OpCode(ULAOpCode), .saida(R[31]), .vem1(ulacell_1_vai1));
  Ulacell ulacell_3 (
    .vai1(ulacell_3_vai1), .a(shiftrightarith32bit_2_out_3[30]), .b(shiftrightarith32bit_1_out_3[29]),
    .OpCode(ULAOpCode), .saida(R[29]), .vem1(ulacell_5_vai1));
  Ulacell ulacell_4 (
    .vai1(ulacell_4_vai1), .a(shiftrightarith32bit_2_out_3[30]), .b(shiftrightarith32bit_1_out_3[27]),
    .OpCode(ULAOpCode), .saida(R[27]), .vem1(ulacell_6_vai1));
  Ulacell ulacell_5 (
    .vai1(ulacell_5_vai1), .a(shiftrightarith32bit_2_out_3[30]), .b(shiftrightarith32bit_1_out_3[28]),
    .OpCode(ULAOpCode), .saida(R[28]), .vem1(ulacell_4_vai1));
  Ulacell ulacell_6 (
    .vai1(ulacell_6_vai1), .a(shiftrightarith32bit_2_out_3[30]), .b(shiftrightarith32bit_1_out_3[26]),
    .OpCode(ULAOpCode), .saida(R[26]), .vem1(ulacell_7_vai1));
  Ulacell ulacell_7 (
    .vai1(ulacell_7_vai1), .a(shiftrightarith32bit_2_out_3[30]), .b(shiftrightarith32bit_1_out_3[25]),
    .OpCode(ULAOpCode), .saida(R[25]), .vem1(ulacell_8_vai1));
  Ulacell ulacell_8 (
    .vai1(ulacell_8_vai1), .a(shiftrightarith32bit_2_out_3[30]), .b(shiftrightarith32bit_1_out_3[24]),
    .OpCode(ULAOpCode), .saida(R[24]), .vem1(ulacell_9_vai1));
  Ulacell ulacell_9 (
    .vai1(ulacell_9_vai1), .a(shiftrightarith32bit_2_out_3[30]), .b(shiftrightarith32bit_1_out_3[23]),
    .OpCode(ULAOpCode), .saida(R[23]), .vem1(ulacell_10_vai1));
  Ulacell ulacell_10 (
    .vai1(ulacell_10_vai1), .a(shiftrightarith32bit_2_out_3[30]), .b(shiftrightarith32bit_1_out_3[22]),
    .OpCode(ULAOpCode), .saida(R[22]), .vem1(ulacell_11_vai1));
  Ulacell ulacell_11 (
    .vai1(ulacell_11_vai1), .a(shiftrightarith32bit_2_out_3[30]), .b(shiftrightarith32bit_1_out_3[21]),
    .OpCode(ULAOpCode), .saida(R[21]), .vem1(ulacell_12_vai1));
  Ulacell ulacell_12 (
    .vai1(ulacell_12_vai1), .a(shiftrightarith32bit_2_out_3[30]), .b(shiftrightarith32bit_1_out_3[20]),
    .OpCode(ULAOpCode), .saida(R[20]), .vem1(ulacell_13_vai1));
  Ulacell ulacell_13 (
    .vai1(ulacell_13_vai1), .a(shiftrightarith32bit_2_out_3[30]), .b(shiftrightarith32bit_1_out_3[19]),
    .OpCode(ULAOpCode), .saida(R[19]), .vem1(ulacell_14_vai1));
  Ulacell ulacell_14 (
    .vai1(ulacell_14_vai1), .a(shiftrightarith32bit_2_out_3[30]), .b(shiftrightarith32bit_1_out_3[18]),
    .OpCode(ULAOpCode), .saida(R[18]), .vem1(ulacell_15_vai1));
  Ulacell ulacell_15 (
    .vai1(ulacell_15_vai1), .a(shiftrightarith32bit_2_out_3[30]), .b(shiftrightarith32bit_1_out_3[17]),
    .OpCode(ULAOpCode), .saida(R[17]), .vem1(ulacell_16_vai1));
  Ulacell ulacell_16 (
    .vai1(ulacell_16_vai1), .a(shiftrightarith32bit_2_out_3[30]), .b(shiftrightarith32bit_1_out_3[16]),
    .OpCode(ULAOpCode), .saida(R[16]), .vem1(ulacell_17_vai1));
  Ulacell ulacell_17 (
    .vai1(ulacell_17_vai1), .a(shiftrightarith32bit_2_out_3[30]), .b(shiftrightarith32bit_1_out_3[15]),
    .OpCode(ULAOpCode), .saida(R[15]), .vem1(ulacell_18_vai1));
  Ulacell ulacell_18 (
    .vai1(ulacell_18_vai1), .a(shiftrightarith32bit_2_out_3[30]), .b(shiftrightarith32bit_1_out_3[14]),
    .OpCode(ULAOpCode), .saida(R[14]), .vem1(ulacell_19_vai1));
  Ulacell ulacell_19 (
    .vai1(ulacell_19_vai1), .a(shiftrightarith32bit_2_out_3[30]), .b(shiftrightarith32bit_1_out_3[13]),
    .OpCode(ULAOpCode), .saida(R[13]), .vem1(ulacell_20_vai1));
  Ulacell ulacell_20 (
    .vai1(ulacell_20_vai1), .a(shiftrightarith32bit_2_out_3[30]), .b(shiftrightarith32bit_1_out_3[12]),
    .OpCode(ULAOpCode), .saida(R[12]), .vem1(ulacell_21_vai1));
  Ulacell ulacell_21 (
    .vai1(ulacell_21_vai1), .a(shiftrightarith32bit_2_out_3[30]), .b(shiftrightarith32bit_1_out_3[11]),
    .OpCode(ULAOpCode), .saida(R[11]), .vem1(ulacell_23_vai1));
  Ulacell ulacell_22 (
    .vai1(ulacell_22_vai1), .a(shiftrightarith32bit_2_out_3[30]), .b(shiftrightarith32bit_1_out_3[9]),
    .OpCode(ULAOpCode), .saida(R[9]), .vem1(ulacell_24_vai1));
  Ulacell ulacell_23 (
    .vai1(ulacell_23_vai1), .a(shiftrightarith32bit_2_out_3[30]), .b(shiftrightarith32bit_1_out_3[10]),
    .OpCode(ULAOpCode), .saida(R[10]), .vem1(ulacell_22_vai1));
  Ulacell ulacell_24 (
    .vai1(ulacell_24_vai1), .a(shiftrightarith32bit_2_out_3[30]), .b(shiftrightarith32bit_1_out_3[8]),
    .OpCode(ULAOpCode), .saida(R[8]), .vem1(ulacell_25_vai1));
  Ulacell ulacell_25 (
    .vai1(ulacell_25_vai1), .a(shiftrightarith32bit_2_out_3[30]), .b(shiftrightarith32bit_1_out_3[7]),
    .OpCode(ULAOpCode), .saida(R[7]), .vem1(ulacell_26_vai1));
  Ulacell ulacell_26 (
    .vai1(ulacell_26_vai1), .a(shiftrightarith32bit_2_out_3[30]), .b(shiftrightarith32bit_1_out_3[6]),
    .OpCode(ULAOpCode), .saida(R[6]), .vem1(ulacell_27_vai1));
  Ulacell ulacell_27 (
    .vai1(ulacell_27_vai1), .a(shiftrightarith32bit_2_out_3[30]), .b(shiftrightarith32bit_1_out_3[5]),
    .OpCode(ULAOpCode), .saida(R[5]), .vem1(ulacell_28_vai1));
  Ulacell ulacell_28 (
    .vai1(ulacell_28_vai1), .a(shiftrightarith32bit_2_out_3[30]), .b(shiftrightarith32bit_1_out_3[4]),
    .OpCode(ULAOpCode), .saida(R[4]), .vem1(ulacell_29_vai1));
  Ulacell ulacell_29 (
    .vai1(ulacell_29_vai1), .a(shiftrightarith32bit_2_out_3[30]), .b(shiftrightarith32bit_1_out_3[3]),
    .OpCode(ULAOpCode), .saida(R[3]), .vem1(ulacell_30_vai1));
  Ulacell ulacell_30 (
    .vai1(ulacell_30_vai1), .a(shiftrightarith32bit_2_out_3[30]), .b(shiftrightarith32bit_1_out_3[2]),
    .OpCode(ULAOpCode), .saida(R[2]), .vem1(ulacell_31_vai1));
  Ulacell ulacell_31 (
    .vai1(ulacell_31_vai1), .a(shiftrightarith32bit_2_out_3[30]), .b(shiftrightarith32bit_1_out_3[1]),
    .OpCode(ULAOpCode), .saida(R[1]), .vem1(ulacell_32_vai1));
  Ulacell ulacell_32 (
    .vai1(ulacell_32_vai1), .a(shiftrightarith32bit_2_out_3[30]), .b(shiftrightarith32bit_1_out_3[0]),
    .OpCode(ULAOpCode), .saida(R[0]), .vem1(1'b0));

  // Notes on the sheet:
  //   00001 - OR
  //   10010 - A
  //   10011 - B
  //   00000 - AND
  //   00010 - SOMADOR
  //   00011 - XOR
  //   00100 - SLL A
  //   00101 - SLL B
  //   00110 - SRL A
  //   00111 - SRL B
  //   01000 - SLA A
  //   01001 - SLA B
  //   01010 - SRA A
  //   01011 - SRA B
  //   01100 - NAND
  //   01101 - NOR
  //   01110 - XNOR
  //   01111 - NOT A
  //   10000 - NOT B
  //   10001 - NOT A+B
endmodule

module Ulafinal (
  input  [31:0] A,
  input  [31:0] B,
  input  [4:0] ULA_OpCode,
  output out_4,
  output out_5,
  output [31:0] Out
);

  wire slaadetector_1_out_2, slabdetector_1_out_2, slladetector_1_out_2, sllbdetector_1_saida,
       sraadetector_1_out_2, srabdetector_1_out_2, srladetector_1_out_2, srlbdetector_1_out_2,
       ulacell_1_vai1, ulacell_3_vai1, ulacell_4_vai1, ulacell_5_vai1, ulacell_6_vai1, ulacell_7_vai1,
       ulacell_8_vai1, ulacell_9_vai1, ulacell_10_vai1, ulacell_11_vai1, ulacell_12_vai1, ulacell_13_vai1,
       ulacell_14_vai1, ulacell_15_vai1, ulacell_16_vai1, ulacell_17_vai1, ulacell_18_vai1, ulacell_19_vai1,
       ulacell_20_vai1, ulacell_21_vai1, ulacell_22_vai1, ulacell_23_vai1, ulacell_24_vai1, ulacell_25_vai1,
       ulacell_26_vai1, ulacell_27_vai1, ulacell_28_vai1, ulacell_29_vai1, ulacell_30_vai1, ulacell_31_vai1,
       ulacell_32_vai1;
  wire [31:0] shiftleftarith32bit_1_out_3, shiftleftarith32bit_2_out_3, shiftleftlogical32bit_1_out_3,
       shiftleftlogical32bit_2_out_3, shiftrightarith32bit_1_out_3, shiftrightarith32bit_2_out_3,
       shiftrightlogical32bit_1_out_3, shiftrightlogical32bit_2_out_3;

  ShiftLeftLogical32bit shiftleftlogical32bit_1 (
    .in_1(A), .Shift(slladetector_1_out_2), .out_3(shiftleftlogical32bit_1_out_3));
  SLLADetector slladetector_1 (.out_2(slladetector_1_out_2), .UlaOpCode(ULA_OpCode));
  ShiftLeftLogical32bit shiftleftlogical32bit_2 (
    .in_1(B), .Shift(sllbdetector_1_saida), .out_3(shiftleftlogical32bit_2_out_3));
  SRLBDetector srlbdetector_1 (.out_2(srlbdetector_1_out_2), .UlaOpCode(ULA_OpCode));
  SLLBDetector sllbdetector_1 (.saida(sllbdetector_1_saida), .UlaOpCode(ULA_OpCode));
  ShiftRightLogical32bit shiftrightlogical32bit_1 (
    .in_1(shiftleftlogical32bit_1_out_3), .Shift(srladetector_1_out_2), .out_3(shiftrightlogical32bit_1_out_3));
  SRLADetector srladetector_1 (.out_2(srladetector_1_out_2), .UlaOpCode(ULA_OpCode));
  SLAADetector slaadetector_1 (.out_2(slaadetector_1_out_2), .UlaOpCode(ULA_OpCode));
  ShiftRightLogical32bit shiftrightlogical32bit_2 (
    .in_1(shiftleftlogical32bit_2_out_3), .Shift(srlbdetector_1_out_2), .out_3(shiftrightlogical32bit_2_out_3));
  ShiftLeftArith32bit shiftleftarith32bit_1 (
    .in_1(shiftrightlogical32bit_2_out_3), .Shift(slabdetector_1_out_2), .out_3(shiftleftarith32bit_1_out_3));
  SLABDetector slabdetector_1 (.out_2(slabdetector_1_out_2), .UlaOpCode(ULA_OpCode));
  ShiftLeftArith32bit shiftleftarith32bit_2 (
    .in_1(shiftrightlogical32bit_1_out_3), .Shift(slaadetector_1_out_2), .out_3(shiftleftarith32bit_2_out_3));
  ShiftRightArith32bit shiftrightarith32bit_1 (
    .in_1(shiftleftarith32bit_2_out_3), .Shift(sraadetector_1_out_2), .out_3(shiftrightarith32bit_1_out_3));
  SRAADetector sraadetector_1 (.out_2(sraadetector_1_out_2), .UlaOpCode(ULA_OpCode));
  ShiftRightArith32bit shiftrightarith32bit_2 (
    .in_1(shiftleftarith32bit_1_out_3), .Shift(srabdetector_1_out_2), .out_3(shiftrightarith32bit_2_out_3));
  SRABDetector srabdetector_1 (.out_2(srabdetector_1_out_2), .UlaOpCode(ULA_OpCode));
  Ulacell ulacell_1 (
    .vai1(ulacell_1_vai1), .a(shiftrightarith32bit_2_out_3[30]), .b(shiftrightarith32bit_1_out_3[30]),
    .OpCode(ULA_OpCode), .saida(Out[30]), .vem1(ulacell_3_vai1));
  Ulacell ulacell_2 (
    .vai1(out_5), .a(shiftrightarith32bit_2_out_3[31]), .b(shiftrightarith32bit_1_out_3[31]),
    .OpCode(ULA_OpCode), .saida(Out[31]), .vem1(ulacell_1_vai1));
  Ulacell ulacell_3 (
    .vai1(ulacell_3_vai1), .a(shiftrightarith32bit_2_out_3[29]), .b(shiftrightarith32bit_1_out_3[29]),
    .OpCode(ULA_OpCode), .saida(Out[29]), .vem1(ulacell_4_vai1));
  Ulacell ulacell_4 (
    .vai1(ulacell_4_vai1), .a(shiftrightarith32bit_2_out_3[28]), .b(shiftrightarith32bit_1_out_3[28]),
    .OpCode(ULA_OpCode), .saida(Out[28]), .vem1(ulacell_5_vai1));
  Ulacell ulacell_5 (
    .vai1(ulacell_5_vai1), .a(shiftrightarith32bit_2_out_3[27]), .b(shiftrightarith32bit_1_out_3[27]),
    .OpCode(ULA_OpCode), .saida(Out[27]), .vem1(ulacell_7_vai1));
  Ulacell ulacell_6 (
    .vai1(ulacell_6_vai1), .a(shiftrightarith32bit_2_out_3[25]), .b(shiftrightarith32bit_1_out_3[25]),
    .OpCode(ULA_OpCode), .saida(Out[25]), .vem1(ulacell_8_vai1));
  Ulacell ulacell_7 (
    .vai1(ulacell_7_vai1), .a(shiftrightarith32bit_2_out_3[26]), .b(shiftrightarith32bit_1_out_3[26]),
    .OpCode(ULA_OpCode), .saida(Out[26]), .vem1(ulacell_6_vai1));
  Ulacell ulacell_8 (
    .vai1(ulacell_8_vai1), .a(shiftrightarith32bit_2_out_3[24]), .b(shiftrightarith32bit_1_out_3[24]),
    .OpCode(ULA_OpCode), .saida(Out[24]), .vem1(ulacell_9_vai1));
  Ulacell ulacell_9 (
    .vai1(ulacell_9_vai1), .a(shiftrightarith32bit_2_out_3[23]), .b(shiftrightarith32bit_1_out_3[23]),
    .OpCode(ULA_OpCode), .saida(Out[23]), .vem1(ulacell_10_vai1));
  Ulacell ulacell_10 (
    .vai1(ulacell_10_vai1), .a(shiftrightarith32bit_2_out_3[22]), .b(shiftrightarith32bit_1_out_3[22]),
    .OpCode(ULA_OpCode), .saida(Out[22]), .vem1(ulacell_11_vai1));
  Ulacell ulacell_11 (
    .vai1(ulacell_11_vai1), .a(shiftrightarith32bit_2_out_3[21]), .b(shiftrightarith32bit_1_out_3[21]),
    .OpCode(ULA_OpCode), .saida(Out[21]), .vem1(ulacell_13_vai1));
  Ulacell ulacell_12 (
    .vai1(ulacell_12_vai1), .a(shiftrightarith32bit_2_out_3[19]), .b(shiftrightarith32bit_1_out_3[19]),
    .OpCode(ULA_OpCode), .saida(Out[19]), .vem1(ulacell_14_vai1));
  Ulacell ulacell_13 (
    .vai1(ulacell_13_vai1), .a(shiftrightarith32bit_2_out_3[20]), .b(shiftrightarith32bit_1_out_3[20]),
    .OpCode(ULA_OpCode), .saida(Out[20]), .vem1(ulacell_12_vai1));
  Ulacell ulacell_14 (
    .vai1(ulacell_14_vai1), .a(shiftrightarith32bit_2_out_3[18]), .b(shiftrightarith32bit_1_out_3[18]),
    .OpCode(ULA_OpCode), .saida(Out[18]), .vem1(ulacell_15_vai1));
  Ulacell ulacell_15 (
    .vai1(ulacell_15_vai1), .a(shiftrightarith32bit_2_out_3[17]), .b(shiftrightarith32bit_1_out_3[17]),
    .OpCode(ULA_OpCode), .saida(Out[17]), .vem1(ulacell_16_vai1));
  Ulacell ulacell_16 (
    .vai1(ulacell_16_vai1), .a(shiftrightarith32bit_2_out_3[16]), .b(shiftrightarith32bit_1_out_3[16]),
    .OpCode(ULA_OpCode), .saida(Out[16]), .vem1(ulacell_18_vai1));
  Ulacell ulacell_17 (
    .vai1(ulacell_17_vai1), .a(shiftrightarith32bit_2_out_3[14]), .b(shiftrightarith32bit_1_out_3[14]),
    .OpCode(ULA_OpCode), .saida(Out[14]), .vem1(ulacell_19_vai1));
  Ulacell ulacell_18 (
    .vai1(ulacell_18_vai1), .a(shiftrightarith32bit_2_out_3[15]), .b(shiftrightarith32bit_1_out_3[15]),
    .OpCode(ULA_OpCode), .saida(Out[15]), .vem1(ulacell_17_vai1));
  Ulacell ulacell_19 (
    .vai1(ulacell_19_vai1), .a(shiftrightarith32bit_2_out_3[13]), .b(shiftrightarith32bit_1_out_3[13]),
    .OpCode(ULA_OpCode), .saida(Out[13]), .vem1(ulacell_20_vai1));
  Ulacell ulacell_20 (
    .vai1(ulacell_20_vai1), .a(shiftrightarith32bit_2_out_3[12]), .b(shiftrightarith32bit_1_out_3[12]),
    .OpCode(ULA_OpCode), .saida(Out[12]), .vem1(ulacell_21_vai1));
  Ulacell ulacell_21 (
    .vai1(ulacell_21_vai1), .a(shiftrightarith32bit_2_out_3[11]), .b(shiftrightarith32bit_1_out_3[11]),
    .OpCode(ULA_OpCode), .saida(Out[11]), .vem1(ulacell_22_vai1));
  Ulacell ulacell_22 (
    .vai1(ulacell_22_vai1), .a(shiftrightarith32bit_2_out_3[10]), .b(shiftrightarith32bit_1_out_3[10]),
    .OpCode(ULA_OpCode), .saida(Out[10]), .vem1(ulacell_23_vai1));
  Ulacell ulacell_23 (
    .vai1(ulacell_23_vai1), .a(shiftrightarith32bit_2_out_3[9]), .b(shiftrightarith32bit_1_out_3[9]),
    .OpCode(ULA_OpCode), .saida(Out[9]), .vem1(ulacell_24_vai1));
  Ulacell ulacell_24 (
    .vai1(ulacell_24_vai1), .a(shiftrightarith32bit_2_out_3[8]), .b(shiftrightarith32bit_1_out_3[8]),
    .OpCode(ULA_OpCode), .saida(Out[8]), .vem1(ulacell_25_vai1));
  Ulacell ulacell_25 (
    .vai1(ulacell_25_vai1), .a(shiftrightarith32bit_2_out_3[7]), .b(shiftrightarith32bit_1_out_3[7]),
    .OpCode(ULA_OpCode), .saida(Out[7]), .vem1(ulacell_26_vai1));
  Ulacell ulacell_26 (
    .vai1(ulacell_26_vai1), .a(shiftrightarith32bit_2_out_3[6]), .b(shiftrightarith32bit_1_out_3[6]),
    .OpCode(ULA_OpCode), .saida(Out[6]), .vem1(ulacell_27_vai1));
  Ulacell ulacell_27 (
    .vai1(ulacell_27_vai1), .a(shiftrightarith32bit_2_out_3[5]), .b(shiftrightarith32bit_1_out_3[5]),
    .OpCode(ULA_OpCode), .saida(Out[5]), .vem1(ulacell_28_vai1));
  Ulacell ulacell_28 (
    .vai1(ulacell_28_vai1), .a(shiftrightarith32bit_2_out_3[4]), .b(shiftrightarith32bit_1_out_3[4]),
    .OpCode(ULA_OpCode), .saida(Out[4]), .vem1(ulacell_29_vai1));
  Ulacell ulacell_29 (
    .vai1(ulacell_29_vai1), .a(shiftrightarith32bit_2_out_3[3]), .b(shiftrightarith32bit_1_out_3[3]),
    .OpCode(ULA_OpCode), .saida(Out[3]), .vem1(ulacell_31_vai1));
  Ulacell ulacell_30 (
    .vai1(ulacell_30_vai1), .a(shiftrightarith32bit_2_out_3[1]), .b(shiftrightarith32bit_1_out_3[1]),
    .OpCode(ULA_OpCode), .saida(Out[1]), .vem1(ulacell_32_vai1));
  Ulacell ulacell_31 (
    .vai1(ulacell_31_vai1), .a(shiftrightarith32bit_2_out_3[2]), .b(shiftrightarith32bit_1_out_3[2]),
    .OpCode(ULA_OpCode), .saida(Out[2]), .vem1(ulacell_30_vai1));
  Ulacell ulacell_32 (
    .vai1(ulacell_32_vai1), .a(shiftrightarith32bit_2_out_3[0]), .b(shiftrightarith32bit_1_out_3[0]),
    .OpCode(ULA_OpCode), .saida(Out[0]), .vem1(1'b0));
  and and_1 (out_4, ~Out[31], ~Out[30], ~Out[29], ~Out[28], ~Out[27], ~Out[26], ~Out[25], ~Out[24], ~Out[23], ~Out[22], ~Out[21], ~Out[20], ~Out[19], ~Out[18], ~Out[17], ~Out[16], ~Out[15], ~Out[14], ~Out[13], ~Out[12], ~Out[11], ~Out[10], ~Out[9], ~Out[8], ~Out[7], ~Out[6], ~Out[5], ~Out[4], ~Out[3], ~Out[2], ~Out[1], ~Out[0]);  // AND_Gate

  // Notes on the sheet:
  //   00000 - AND
  //   00001 - OR
  //   00010 - SOMADOR
  //   00011 - XOR
  //   00100 - SLL A
  //   00101 - SLL B
  //   00110 - SRL A
  //   00111 - SRL B
  //   01000 - SLA A
  //   01001 - SLA B
  //   01010 - SRA A
  //   01011 - SRA B
  //   01100 - NAND
  //   01101 - NOR
  //   01110 - XNOR
  //   01111 - NOT A
  //   10000 - NOT B
  //   10001 - NOT A+B
  //   10010 - A
  //   10011 - B
  //   11111 - ZERO
endmodule

module projeto (
  input  [31:0] A,
  input  [31:0] B,
  input  [4:0] OP,
  output ZERO,
  output [31:0] R,
  output out_6
);

  Hex_Digit_Display hex_digit_display_1 (.value(A[31:28]));  // open: dp
  Hex_Digit_Display hex_digit_display_2 (.value(B[31:28]));  // open: dp
  Hex_Digit_Display hex_digit_display_3 (.value(A[23:20]));  // open: dp
  Hex_Digit_Display hex_digit_display_4 (.value(A[27:24]));  // open: dp
  Hex_Digit_Display hex_digit_display_5 (.value(B[23:20]));  // open: dp
  Hex_Digit_Display hex_digit_display_6 (.value(B[27:24]));  // open: dp
  Hex_Digit_Display hex_digit_display_7 (.value(A[19:16]));  // open: dp
  Hex_Digit_Display hex_digit_display_8 (.value(A[15:12]));  // open: dp
  Hex_Digit_Display hex_digit_display_9 (.value(B[19:16]));  // open: dp
  Hex_Digit_Display hex_digit_display_10 (.value(B[15:12]));  // open: dp
  Hex_Digit_Display hex_digit_display_11 (.value(A[7:4]));  // open: dp
  Hex_Digit_Display hex_digit_display_12 (.value(A[11:8]));  // open: dp
  Hex_Digit_Display hex_digit_display_13 (.value(B[7:4]));  // open: dp
  Hex_Digit_Display hex_digit_display_14 (.value(B[11:8]));  // open: dp
  Hex_Digit_Display hex_digit_display_15 (.value(A[3:0]));  // open: dp
  Ulafinal ulafinal_1 (.A(A), .B(B), .out_5(out_6), .Out(R), .ULA_OpCode(OP), .out_4(ZERO));
  Hex_Digit_Display hex_digit_display_16 (.value(B[3:0]));  // open: dp
  Hex_Digit_Display hex_digit_display_17 (.value(R[31:28]));  // open: dp
  Hex_Digit_Display hex_digit_display_18 (.value(R[27:24]));  // open: dp
  Hex_Digit_Display hex_digit_display_19 (.value(R[19:16]));  // open: dp
  Hex_Digit_Display hex_digit_display_20 (.value(R[23:20]));  // open: dp
  Hex_Digit_Display hex_digit_display_21 (.value(R[15:12]));  // open: dp
  Hex_Digit_Display hex_digit_display_22 (.value(R[11:8]));  // open: dp
  Hex_Digit_Display hex_digit_display_23 (.value(R[7:4]));  // open: dp
  Hex_Digit_Display hex_digit_display_24 (.value(R[3:0]));  // open: dp

  // Notes on the sheet:
  //   00000 - AND
  //   00001 - OR
  //   00010 - SOMADOR
  //   00011 - XOR
  //   00100 - SLL A
  //   00101 - SLL B
  //   00110 - SRL A
  //   00111 - SRL B
  //   01000 - SLA A
  //   01001 - SLA B
  //   01010 - SRA A
  //   01011 - SRA B
  //   01100 - NAND
  //   01101 - NOR
  //   01110 - XNOR
  //   01111 - NOT B
  //   10000 - NOT A
  //   10001 - NOT A+B
  //   10010 - B
  //   10011 - A
  //   11111 - ZERO
endmodule
