// Logisim project banco_Braulio.circ as structural Verilog: 4 circuits, main circuit main
module main (
  input  in_1,
  input  in_2,
  input  [9:0] Instruction
);

  wire [3:0] banco8reg4bits_1_viewrega, banco8reg4bits_1_viewregb, ula_1_s;

  Banco8Reg4bits banco8reg4bits_1 (
    .CLK(in_1), .Data(ula_1_s), .WReg(Instruction[8:6]), .Reset(in_2), .RegA(Instruction[5:3]),
    .RegB(Instruction[2:0]), .ViewRegA(banco8reg4bits_1_viewrega), .ViewRegB(banco8reg4bits_1_viewregb));
  ULA ula_1 (.A(banco8reg4bits_1_viewrega), .B(banco8reg4bits_1_viewregb), .OpCode(Instruction[9]), .S(ula_1_s));
endmodule

module Registrador4bits (
  input  [3:0] DataIN,
  input  Save,
  input  Reset,
  output [3:0] DataOUT
);

  D_Flip_Flop d_ff_1 (.clk(Save), .D(DataIN[3]), .Q(DataOUT[3]), .reset(Reset));  // open: Qn, preset, en
  D_Flip_Flop d_ff_2 (.clk(Save), .D(DataIN[2]), .Q(DataOUT[2]), .reset(Reset));  // open: Qn, preset, en
  D_Flip_Flop d_ff_3 (.clk(Save), .D(DataIN[1]), .Q(DataOUT[1]), .reset(Reset));  // open: Qn, preset, en
  D_Flip_Flop d_ff_4 (.clk(Save), .D(DataIN[0]), .Q(DataOUT[0]), .reset(Reset));  // open: Qn, preset, en
endmodule

module Banco8Reg4bits (
  input  [3:0] Data,
  input  Reset,
  input  [2:0] RegA,
  input  CLK,
  input  [2:0] WReg,
  input  [2:0] RegB,
  output [3:0] ViewRegA,
  output [3:0] ViewRegB
);

  wire demultiplexer_1_out0, demultiplexer_1_out1, demultiplexer_1_out2, demultiplexer_1_out3,
       demultiplexer_1_out4, demultiplexer_1_out5, demultiplexer_1_out6, demultiplexer_1_out7;
  wire [3:0] registrador4bits_1_dataout, registrador4bits_2_dataout, registrador4bits_3_dataout,
       registrador4bits_4_dataout, registrador4bits_5_dataout, registrador4bits_6_dataout,
       registrador4bits_7_dataout, registrador4bits_8_dataout;

  Demultiplexer #(.select(3), .enable("false")) demultiplexer_1 (
    .out0(demultiplexer_1_out0), .out1(demultiplexer_1_out1), .out2(demultiplexer_1_out2),
    .out3(demultiplexer_1_out3), .out4(demultiplexer_1_out4), .out5(demultiplexer_1_out5),
    .out6(demultiplexer_1_out6), .out7(demultiplexer_1_out7), .in(CLK), .sel(WReg));
  Registrador4bits registrador4bits_1 (
    .DataIN(Data), .Save(demultiplexer_1_out0), .Reset(Reset), .DataOUT(registrador4bits_1_dataout));
  Registrador4bits registrador4bits_2 (
    .DataIN(Data), .Save(demultiplexer_1_out1), .Reset(Reset), .DataOUT(registrador4bits_2_dataout));
  Registrador4bits registrador4bits_3 (
    .DataIN(Data), .Save(demultiplexer_1_out2), .Reset(Reset), .DataOUT(registrador4bits_3_dataout));
  Registrador4bits registrador4bits_4 (
    .DataIN(Data), .Save(demultiplexer_1_out3), .Reset(Reset), .DataOUT(registrador4bits_4_dataout));
  Registrador4bits registrador4bits_5 (
    .DataIN(Data), .Save(demultiplexer_1_out4), .Reset(Reset), .DataOUT(registrador4bits_5_dataout));
  Registrador4bits registrador4bits_6 (
    .DataIN(Data), .Save(demultiplexer_1_out5), .Reset(Reset), .DataOUT(registrador4bits_6_dataout));
  Registrador4bits registrador4bits_7 (
    .DataIN(Data), .Save(demultiplexer_1_out6), .Reset(Reset), .DataOUT(registrador4bits_7_dataout));
  Registrador4bits registrador4bits_8 (
    .DataIN(Data), .Save(demultiplexer_1_out7), .Reset(Reset), .DataOUT(registrador4bits_8_dataout));
  Multiplexer #(.select(3), .width(4), .enable("false")) multiplexer_1 (
    .in0(registrador4bits_1_dataout), .in1(registrador4bits_2_dataout), .in2(registrador4bits_3_dataout),
    .in3(registrador4bits_4_dataout), .in4(registrador4bits_5_dataout), .in5(registrador4bits_6_dataout),
    .in6(registrador4bits_7_dataout), .in7(registrador4bits_8_dataout), .out(ViewRegA), .sel(RegA));
  Multiplexer #(.select(3), .width(4), .enable("false")) multiplexer_2 (
    .in0(registrador4bits_1_dataout), .in1(registrador4bits_2_dataout), .in2(registrador4bits_3_dataout),
    .in3(registrador4bits_4_dataout), .in4(registrador4bits_5_dataout), .in5(registrador4bits_6_dataout),
    .in6(registrador4bits_7_dataout), .in7(registrador4bits_8_dataout), .out(ViewRegB), .sel(RegB));
endmodule

module ULA (
  input  [3:0] A,
  input  [3:0] B,
  input  OpCode,
  output [3:0] S
);

  wire [3:0] adder_1_out, and_1_out;

  assign and_1_out = A & B;  // AND_Gate and_1, 4 bits wide
  Adder #(.width(4)) adder_1 (.a(A), .b(B), .out(adder_1_out), .cin(1'b0));  // open: cout
  Multiplexer #(.width(4), .enable("false")) multiplexer_1 (.in0(and_1_out), .in1(adder_1_out), .out(S), .sel(OpCode));
endmodule
